// Logisim project Forwarding_unit.circ as structural Verilog: 1 circuit, main circuit Unit
module Unit (
  input  EX_MEM_RegWrite,
  input  [4:0] EX_MEM_RegisterRd,
  input  [4:0] ID_EX_RegisterRs,
  input  [4:0] ID_EX_RegisterRt,
  input  MEM_WB_RegWrite,
  input  [4:0] MEM_WB_RegisterRd,
  output [1:0] ForwardA,
  output [1:0] ForwardB
);

  wire and_1_out, and_2_out, and_3_out, and_4_out, comparator_1_eq, comparator_2_eq, comparator_3_eq,
       comparator_4_eq, comparator_5_eq, comparator_6_eq, comparator_7_eq, comparator_8_eq, not_1_out,
       not_2_out, not_3_out, not_4_out;
  wire [1:0] multiplexer_1_out, multiplexer_2_out, multiplexer_3_out, multiplexer_4_out;

  not not_1 (not_1_out, comparator_1_eq);
  Comparator #(.width(5)) comparator_1 (.a(EX_MEM_RegisterRd), .b({5{1'b0}}), .eq(comparator_1_eq));  // open: gt, lt
  Comparator #(.width(5)) comparator_2 (
    .a(EX_MEM_RegisterRd), .b(ID_EX_RegisterRs), .eq(comparator_2_eq));  // open: gt, lt
  Comparator #(.width(5)) comparator_3 (
    .a(EX_MEM_RegisterRd), .b(ID_EX_RegisterRt), .eq(comparator_3_eq));  // open: gt, lt
  not not_2 (not_2_out, comparator_4_eq);
  Comparator #(.width(5)) comparator_4 (.a(MEM_WB_RegisterRd), .b({5{1'b0}}), .eq(comparator_4_eq));  // open: gt, lt
  not not_3 (not_3_out, comparator_5_eq);
  Comparator #(.width(5)) comparator_5 (
    .a(ID_EX_RegisterRs), .b(EX_MEM_RegisterRd), .eq(comparator_5_eq));  // open: gt, lt
  Comparator #(.width(5)) comparator_6 (
    .a(MEM_WB_RegisterRd), .b(ID_EX_RegisterRs), .eq(comparator_6_eq));  // open: gt, lt
  not not_4 (not_4_out, comparator_7_eq);
  Comparator #(.width(5)) comparator_7 (
    .a(EX_MEM_RegisterRd), .b(ID_EX_RegisterRt), .eq(comparator_7_eq));  // open: gt, lt
  Comparator #(.width(5)) comparator_8 (
    .a(ID_EX_RegisterRt), .b(MEM_WB_RegisterRd), .eq(comparator_8_eq));  // open: gt, lt
  and and_1 (and_1_out, EX_MEM_RegWrite, not_1_out, comparator_2_eq);
  and and_2 (and_2_out, EX_MEM_RegWrite, not_1_out, comparator_3_eq);
  and and_3 (and_3_out, MEM_WB_RegWrite, not_2_out, not_3_out, comparator_6_eq);
  and and_4 (and_4_out, MEM_WB_RegWrite, not_2_out, not_4_out, comparator_8_eq);
  Multiplexer #(.width(2), .enable("false")) multiplexer_1 (
    .in0(2'b00), .in1(2'b10), .out(multiplexer_1_out), .sel(and_1_out));
  Multiplexer #(.width(2), .enable("false")) multiplexer_2 (
    .in0(2'b00), .in1(2'b10), .out(multiplexer_2_out), .sel(and_2_out));
  Multiplexer #(.width(2), .enable("false")) multiplexer_3 (
    .in0(2'b00), .in1(2'b01), .out(multiplexer_3_out), .sel(and_3_out));
  // Probe on 2'b00
  // Probe on 2'b10
  // Probe on 2'b00
  // Probe on 2'b10
  // Probe on 2'b00
  // Probe on 2'b01
  // Probe on 2'b00
  Multiplexer #(.width(2), .enable("false")) multiplexer_4 (
    .in0(2'b00), .in1(2'b01), .out(multiplexer_4_out), .sel(and_4_out));
  // Probe on 2'b01
  // Probe on multiplexer_1_out
  // Probe on multiplexer_4_out
  // Probe on multiplexer_3_out
  // Probe on multiplexer_2_out
  // Probe on ForwardA
  assign ForwardA = multiplexer_1_out | multiplexer_3_out;  // OR_Gate or_1, 2 bits wide
  assign ForwardB = multiplexer_2_out | multiplexer_4_out;  // OR_Gate or_2, 2 bits wide
  // Probe on ForwardB

  // Notes on the sheet:
  //   EX hazar
  //   MEM hazar
endmodule
