// Logisim project Hazard_detector.circ as structural Verilog: 3 circuits, main circuit FullDetector
module FullDetector (
  input  [4:0] Rd,
  input  [4:0] Rs_1,
  input  RegWrite,
  input  [4:0] Rt_1,
  input  [4:0] Rt,
  output out_6
);

  wire and_1_out, comparator_1_eq, comparator_2_eq, comparator_3_eq, comparator_4_eq, comparator_5_eq,
       comparator_6_eq, comparator_7_eq, not_1_out, not_2_out, not_3_out, or_1_out, or_2_out;

  Comparator #(.width(5)) comparator_1 (.a(Rd), .b(Rs_1), .eq(comparator_1_eq));  // open: gt, lt
  Comparator #(.width(5)) comparator_2 (.a(Rd), .b(Rt_1), .eq(comparator_2_eq));  // open: gt, lt
  Comparator #(.width(5)) comparator_3 (.a(Rt), .b(Rt_1), .eq(comparator_3_eq));  // open: gt, lt
  Comparator #(.width(5)) comparator_4 (.a(Rs_1), .b(Rt), .eq(comparator_4_eq));  // open: gt, lt
  Comparator #(.width(5)) comparator_5 (.a(Rd), .b({5{1'b0}}), .eq(comparator_5_eq));  // open: gt, lt
  Comparator #(.width(5)) comparator_6 (.a(Rs_1), .b({5{1'b0}}), .eq(comparator_6_eq));  // open: gt, lt
  Comparator #(.width(5)) comparator_7 (.a(Rt_1), .b({5{1'b0}}), .eq(comparator_7_eq));  // open: gt, lt
  or or_1 (or_1_out, comparator_1_eq, comparator_2_eq, comparator_3_eq, comparator_4_eq);
  not not_1 (not_1_out, comparator_5_eq);
  not not_2 (not_2_out, comparator_6_eq);
  or or_2 (or_2_out, not_1_out, not_2_out, not_3_out);
  not not_3 (not_3_out, comparator_7_eq);
  and and_1 (and_1_out, RegWrite, or_1_out);
  and and_2 (out_6, and_1_out, or_2_out);
endmodule

module Load_use (
  input  ID_EX_MemRead,
  input  [4:0] ID_EX_RegisterRt,
  input  [4:0] IF_ID_RegisterRS,
  input  [4:0] IF_ID_RegisterRt,
  input  [4:0] ID_EX_RegisterRd,
  output Hazard
);

  wire and_1_out, and_2_out, and_3_out, and_4_out, comparator_1_eq, comparator_2_eq, comparator_3_eq,
       comparator_4_eq, comparator_5_eq, comparator_6_eq, comparator_7_eq, comparator_8_eq, not_1_out,
       not_2_out, not_3_out, not_4_out;

  Comparator #(.width(5)) comparator_1 (
    .a(ID_EX_RegisterRt), .b(IF_ID_RegisterRS), .eq(comparator_1_eq));  // open: gt, lt
  Comparator #(.width(5)) comparator_2 (.a(ID_EX_RegisterRt), .b({5{1'b0}}), .eq(comparator_2_eq));  // open: gt, lt
  Comparator #(.width(5)) comparator_3 (.a(ID_EX_RegisterRt), .b({5{1'b0}}), .eq(comparator_3_eq));  // open: gt, lt
  Comparator #(.width(5)) comparator_4 (
    .a(ID_EX_RegisterRt), .b(IF_ID_RegisterRt), .eq(comparator_4_eq));  // open: gt, lt
  Comparator #(.width(5)) comparator_5 (.a(IF_ID_RegisterRt), .b({5{1'b0}}), .eq(comparator_5_eq));  // open: gt, lt
  Comparator #(.width(5)) comparator_6 (.a(ID_EX_RegisterRd), .b({5{1'b0}}), .eq(comparator_6_eq));  // open: gt, lt
  Comparator #(.width(5)) comparator_7 (
    .a(ID_EX_RegisterRd), .b(IF_ID_RegisterRt), .eq(comparator_7_eq));  // open: gt, lt
  Comparator #(.width(5)) comparator_8 (
    .a(IF_ID_RegisterRS), .b(ID_EX_RegisterRd), .eq(comparator_8_eq));  // open: gt, lt
  LED led_1 (.in(comparator_1_eq));
  not not_1 (not_1_out, comparator_2_eq);
  not not_2 (not_2_out, comparator_3_eq);
  LED led_2 (.in(comparator_4_eq));
  not not_3 (not_3_out, comparator_5_eq);
  not not_4 (not_4_out, comparator_7_eq);
  and and_1 (and_1_out, not_1_out, comparator_4_eq, not_3_out);
  and and_2 (and_2_out, comparator_6_eq, not_4_out, comparator_8_eq);
  and and_3 (and_3_out, comparator_1_eq, not_1_out, not_2_out);
  and and_4 (and_4_out, ID_EX_MemRead, and_3_out);
  or or_1 (Hazard, and_4_out, and_1_out, and_2_out);
endmodule

module Load_use_v2 (
  input  ID_EX_MemRead,
  input  [4:0] ID_EX_RegisterRt,
  input  [4:0] IF_ID_RegisterRS,
  input  [4:0] IF_ID_RegisterRt,
  output Hazard
);

  wire and_1_out, comparator_1_eq, comparator_2_eq;

  Comparator #(.width(5)) comparator_1 (
    .a(ID_EX_RegisterRt), .b(IF_ID_RegisterRS), .eq(comparator_1_eq));  // open: gt, lt
  Comparator #(.width(5)) comparator_2 (
    .a(ID_EX_RegisterRt), .b(IF_ID_RegisterRt), .eq(comparator_2_eq));  // open: gt, lt
  LED led_1 (.in(comparator_1_eq));
  LED led_2 (.in(comparator_2_eq));
  and and_1 (and_1_out, ID_EX_MemRead, comparator_1_eq);
  or or_1 (Hazard, and_1_out, comparator_2_eq);
endmodule
