// Logisim project Pipeline.circ as structural Verilog: 4 circuits, main circuit IF/ID
module IF_ID (
  input  Enable,
  input  [31:0] Inst_IF,
  input  Clock,
  input  Clear,
  input  [23:0] PC_ID,
  output [31:0] Inst_ID,
  output [23:0] PC_IF
);

  Register #(.width(32)) register_1 (.D(Inst_IF), .en(Enable), .Q(Inst_ID), .clk(Clock), .clr(Clear));
  Register #(.width(24)) register_2 (.D(PC_ID), .en(Enable), .Q(PC_IF), .clk(Clock), .clr(Clear));
endmodule

module ID_EX (
  input  Clear,
  input  ALUCtrl3_ID,
  input  [15:0] Imm_ID,
  input  [4:0] Shamt_ID,
  input  ALUCtrl2_ID,
  input  ALUSrc_ID,
  input  [31:0] BusA_ID,
  input  [25:0] JumpAddr,
  input  ALUCtrl1_ID,
  input  MemtoReg_ID,
  input  Clock,
  input  ALUCtrl0_ID,
  input  RegWrite_ID,
  input  [31:0] BusB_ID,
  input  [23:0] PC_ID,
  input  Jump_ID,
  input  MemRead_ID,
  input  [4:0] Rd_ID,
  input  [4:0] Rt_ID,
  input  RegDest_ID,
  input  MemWrite_ID,
  input  ALUOP0_ID,
  input  [5:0] Funct_ID,
  input  [4:0] Rs_ID,
  input  Branch_ID,
  input  ALUOP1_ID,
  input  Bne_ID,
  input  [5:0] Op_ID,
  input  Enable,
  output ALUCtrl3_EX,
  output [15:0] Imm_EX,
  output [4:0] Shamt_EX,
  output ALUCtrl2_EX,
  output ALUSrc_EX,
  output [31:0] BusA_EX,
  output [25:0] JumpAddr_2,
  output ALUCtrl1_EX,
  output MemtoReg_EX,
  output ALUCtrl0_EX,
  output RegWrite_EX,
  output [31:0] BusB_EX,
  output [23:0] PC_EX,
  output Jump_EX,
  output MemRead_EX,
  output [4:0] Rd_EX,
  output [4:0] Rt_EX,
  output RegDest_EX,
  output MemWrite_EX,
  output ALUOP0_EX,
  output [5:0] Funct_EX,
  output [4:0] Rs_EX,
  output Branch_EX,
  output ALUOP1_ID_2,
  output Bne_EX,
  output [5:0] Op_EX
);

  Register #(.width(16)) register_1 (.D(Imm_ID), .en(Enable), .Q(Imm_EX), .clk(Clock), .clr(Clear));
  Register #(.width(32)) register_2 (.D(BusA_ID), .en(Enable), .Q(BusA_EX), .clk(Clock), .clr(Clear));
  Register #(.width(32)) register_3 (.D(BusB_ID), .en(Enable), .Q(BusB_EX), .clk(Clock), .clr(Clear));
  Register #(.width(5)) register_4 (.D(Rd_ID), .en(Enable), .Q(Rd_EX), .clk(Clock), .clr(Clear));
  Register #(.width(6)) register_5 (.D(Funct_ID), .en(Enable), .Q(Funct_EX), .clk(Clock), .clr(Clear));
  Register #(.width(6)) register_6 (.D(Op_ID), .en(Enable), .Q(Op_EX), .clk(Clock), .clr(Clear));
  Register #(.width(5)) register_7 (.D(Shamt_ID), .en(Enable), .Q(Shamt_EX), .clk(Clock), .clr(Clear));
  Register #(.width(26)) register_8 (.D(JumpAddr), .en(Enable), .Q(JumpAddr_2), .clk(Clock), .clr(Clear));
  Register #(.width(24)) register_9 (.D(PC_ID), .en(Enable), .Q(PC_EX), .clk(Clock), .clr(Clear));
  Register #(.width(5)) register_10 (.D(Rt_ID), .en(Enable), .Q(Rt_EX), .clk(Clock), .clr(Clear));
  Register #(.width(5)) register_11 (.D(Rs_ID), .en(Enable), .Q(Rs_EX), .clk(Clock), .clr(Clear));
  Register #(.width(1)) register_12 (.D(ALUSrc_ID), .en(Enable), .Q(ALUSrc_EX), .clk(Clock), .clr(Clear));
  Register #(.width(1)) register_13 (.D(MemtoReg_ID), .en(Enable), .Q(MemtoReg_EX), .clk(Clock), .clr(Clear));
  Register #(.width(1)) register_14 (.D(RegWrite_ID), .en(Enable), .Q(RegWrite_EX), .clk(Clock), .clr(Clear));
  Register #(.width(1)) register_15 (.D(MemRead_ID), .en(Enable), .Q(MemRead_EX), .clk(Clock), .clr(Clear));
  Register #(.width(1)) register_16 (.D(MemWrite_ID), .en(Enable), .Q(MemWrite_EX), .clk(Clock), .clr(Clear));
  Register #(.width(1)) register_17 (.D(Branch_ID), .en(Enable), .Q(Branch_EX), .clk(Clock), .clr(Clear));
  Register #(.width(1)) register_18 (.D(Bne_ID), .en(Enable), .Q(Bne_EX), .clk(Clock), .clr(Clear));
  Register #(.width(1)) register_19 (.D(ALUCtrl3_ID), .en(Enable), .Q(ALUCtrl3_EX), .clk(Clock), .clr(Clear));
  Register #(.width(1)) register_20 (.D(ALUCtrl2_ID), .en(Enable), .Q(ALUCtrl2_EX), .clk(Clock), .clr(Clear));
  Register #(.width(1)) register_21 (.D(ALUCtrl1_ID), .en(Enable), .Q(ALUCtrl1_EX), .clk(Clock), .clr(Clear));
  Register #(.width(1)) register_22 (.D(ALUCtrl0_ID), .en(Enable), .Q(ALUCtrl0_EX), .clk(Clock), .clr(Clear));
  Register #(.width(1)) register_23 (.D(Jump_ID), .en(Enable), .Q(Jump_EX), .clk(Clock), .clr(Clear));
  Register #(.width(1)) register_24 (.D(RegDest_ID), .en(Enable), .Q(RegDest_EX), .clk(Clock), .clr(Clear));
  Register #(.width(1)) register_25 (.D(ALUOP0_ID), .en(Enable), .Q(ALUOP0_EX), .clk(Clock), .clr(Clear));
  Register #(.width(1)) register_26 (.D(ALUOP1_ID), .en(Enable), .Q(ALUOP1_ID_2), .clk(Clock), .clr(Clear));
endmodule

module EX_MEM (
  input  Clock,
  input  Clear,
  input  MentoReg_EX,
  input  [31:0] ALUResult_EX,
  input  RegWrite_EX,
  input  MemRead_EX,
  input  [23:0] PC_EX,
  input  MemWrite_EX,
  input  [31:0] BusB_EX,
  input  [4:0] Rd_EX,
  input  [4:0] Rt_EX,
  input  [4:0] Rs_EX,
  input  [5:0] Funct_EX,
  input  RegDest_EX,
  input  ALUOP0_EX,
  input  [4:0] RW_EX,
  input  ALUOP1_EX,
  input  [5:0] Op_EX,
  input  Zero_EX,
  input  Branch_EX,
  input  Enable,
  output MentoReg_MEM,
  output [31:0] ALUResult_MEM,
  output RegWrite_MEM,
  output MemRead_MEM,
  output [23:0] PC_MEM,
  output MemWrite_MEM,
  output [31:0] BusB_MEM,
  output [4:0] Rd_MEM,
  output [4:0] Rt_MEM,
  output [4:0] Rs_MEM,
  output [5:0] Funct_MEM,
  output RegDest_MEM,
  output ALUOP0_MEM,
  output [4:0] RW_MEM,
  output ALUOP1_MEM,
  output [5:0] Op_MEM,
  output Zero_MEM,
  output Branch_MEM
);

  Register #(.width(1)) register_1 (.D(MentoReg_EX), .en(Enable), .Q(MentoReg_MEM), .clk(Clock), .clr(Clear));
  Register #(.width(1)) register_2 (.D(RegWrite_EX), .en(Enable), .Q(RegWrite_MEM), .clk(Clock), .clr(Clear));
  Register #(.width(1)) register_3 (.D(MemRead_EX), .en(Enable), .Q(MemRead_MEM), .clk(Clock), .clr(Clear));
  Register #(.width(1)) register_4 (.D(MemWrite_EX), .en(Enable), .Q(MemWrite_MEM), .clk(Clock), .clr(Clear));
  Register #(.width(5)) register_5 (.D(Rd_EX), .en(Enable), .Q(Rd_MEM), .clk(Clock), .clr(Clear));
  Register #(.width(5)) register_6 (.D(Rt_EX), .en(Enable), .Q(Rt_MEM), .clk(Clock), .clr(Clear));
  Register #(.width(6)) register_7 (.D(Funct_EX), .en(Enable), .Q(Funct_MEM), .clk(Clock), .clr(Clear));
  Register #(.width(5)) register_8 (.D(RW_EX), .en(Enable), .Q(RW_MEM), .clk(Clock), .clr(Clear));
  Register #(.width(6)) register_9 (.D(Op_EX), .en(Enable), .Q(Op_MEM), .clk(Clock), .clr(Clear));
  Register #(.width(32)) register_10 (.D(ALUResult_EX), .en(Enable), .Q(ALUResult_MEM), .clk(Clock), .clr(Clear));
  Register #(.width(24)) register_11 (.D(PC_EX), .en(Enable), .Q(PC_MEM), .clk(Clock), .clr(Clear));
  Register #(.width(32)) register_12 (.D(BusB_EX), .en(Enable), .Q(BusB_MEM), .clk(Clock), .clr(Clear));
  Register #(.width(5)) register_13 (.D(Rs_EX), .en(Enable), .Q(Rs_MEM), .clk(Clock), .clr(Clear));
  Register #(.width(1)) register_14 (.D(RegDest_EX), .en(Enable), .Q(RegDest_MEM), .clk(Clock), .clr(Clear));
  Register #(.width(1)) register_15 (.D(ALUOP0_EX), .en(Enable), .Q(ALUOP0_MEM), .clk(Clock), .clr(Clear));
  Register #(.width(1)) register_16 (.D(ALUOP1_EX), .en(Enable), .Q(ALUOP1_MEM), .clk(Clock), .clr(Clear));
  Register #(.width(1)) register_17 (.D(Zero_EX), .en(Enable), .Q(Zero_MEM), .clk(Clock), .clr(Clear));
  Register #(.width(1)) register_18 (.D(Branch_EX), .en(Enable), .Q(Branch_MEM), .clk(Clock), .clr(Clear));
endmodule

module MEM_WB (
  input  Clock,
  input  Clear,
  input  RegDest_MEM,
  input  [31:0] ALUResult_MEM,
  input  MemtoReg_MEM,
  input  RegWriteMEM,
  input  [31:0] BusW_MEM,
  input  MemRead_MEM,
  input  [23:0] PC_MEM,
  input  [4:0] Rd_MEM,
  input  [4:0] Rs_MEM,
  input  [4:0] Rt_MEM,
  input  ALUOP0_MEM,
  input  [5:0] Funct_MEM,
  input  ALUOP1_MEM,
  input  [4:0] RW_MEM,
  input  [5:0] OP_MEM,
  input  Enable,
  output RegDest_WB,
  output [31:0] ALUResult_WB,
  output MemtoReg_WB,
  output RegWriteWB,
  output [31:0] BusW_WB,
  output MemRead_WB,
  output [23:0] PC_WB,
  output [4:0] Rd_WB,
  output [4:0] Rs_WB,
  output [4:0] Rt_WB,
  output ALUOP0_WB,
  output [5:0] Funct_WB,
  output ALUOP1_WB,
  output [4:0] RW_WB,
  output [5:0] OP_WB
);

  Register #(.width(1)) register_1 (.D(RegDest_MEM), .en(Enable), .Q(RegDest_WB), .clk(Clock), .clr(Clear));
  Register #(.width(1)) register_2 (.D(MemtoReg_MEM), .en(Enable), .Q(MemtoReg_WB), .clk(Clock), .clr(Clear));
  Register #(.width(1)) register_3 (.D(RegWriteMEM), .en(Enable), .Q(RegWriteWB), .clk(Clock), .clr(Clear));
  Register #(.width(1)) register_4 (.D(MemRead_MEM), .en(Enable), .Q(MemRead_WB), .clk(Clock), .clr(Clear));
  Register #(.width(5)) register_5 (.D(Rd_MEM), .en(Enable), .Q(Rd_WB), .clk(Clock), .clr(Clear));
  Register #(.width(5)) register_6 (.D(Rt_MEM), .en(Enable), .Q(Rt_WB), .clk(Clock), .clr(Clear));
  Register #(.width(6)) register_7 (.D(Funct_MEM), .en(Enable), .Q(Funct_WB), .clk(Clock), .clr(Clear));
  Register #(.width(5)) register_8 (.D(RW_MEM), .en(Enable), .Q(RW_WB), .clk(Clock), .clr(Clear));
  Register #(.width(32)) register_9 (.D(ALUResult_MEM), .en(Enable), .Q(ALUResult_WB), .clk(Clock), .clr(Clear));
  Register #(.width(32)) register_10 (.D(BusW_MEM), .en(Enable), .Q(BusW_WB), .clk(Clock), .clr(Clear));
  Register #(.width(24)) register_11 (.D(PC_MEM), .en(Enable), .Q(PC_WB), .clk(Clock), .clr(Clear));
  Register #(.width(5)) register_12 (.D(Rs_MEM), .en(Enable), .Q(Rs_WB), .clk(Clock), .clr(Clear));
  Register #(.width(1)) register_13 (.D(ALUOP0_MEM), .en(Enable), .Q(ALUOP0_WB), .clk(Clock), .clr(Clear));
  Register #(.width(1)) register_14 (.D(ALUOP1_MEM), .en(Enable), .Q(ALUOP1_WB), .clk(Clock), .clr(Clear));
  Register #(.width(6)) register_15 (.D(OP_MEM), .en(Enable), .Q(OP_WB), .clk(Clock), .clr(Clear));
endmodule
