// Logisim project Single-Cycle - Pipeline Processor MIPS.circ as structural Verilog: 38 circuits, main circuit main_pipeline
module main_pipeline (
  output [4:0] out_1
);

  wire alu_1_out_8, alucontrol_1_aluctrl0, alucontrol_1_aluctrl1, alucontrol_1_aluctrl2,
       alucontrol_1_aluctrl3, and_1_out, bne, Branch, Clock, comparator_1_eq, control_1_aluop0,
       control_1_aluop1, control_1_alusrc, control_1_bne, control_1_branch, control_1_jump,
       control_1_memread, control_1_memtoreg, control_1_memwrite, control_1_regdst, control_1_regwrite,
       display2_controller_1_a, display2_controller_1_b, display2_controller_1_c, display2_controller_1_d,
       display2_controller_1_e, display2_controller_1_f, display2_controller_1_g, display2_controller_2_a,
       display2_controller_2_b, display2_controller_2_c, display2_controller_2_d, display2_controller_2_e,
       display2_controller_2_f, display2_controller_2_g, display2_controller_3_a, display2_controller_3_b,
       display2_controller_3_c, display2_controller_3_d, display2_controller_3_e, display2_controller_3_f,
       display2_controller_3_g, display2_controller_4_a, display2_controller_4_b, display2_controller_4_c,
       display2_controller_4_d, display2_controller_4_e, display2_controller_4_f, display2_controller_4_g,
       display3_controller_1_a, display3_controller_1_b, display3_controller_1_c, display3_controller_1_d,
       display3_controller_1_e, display3_controller_1_f, display3_controller_1_g, display3_controller_2_a,
       display3_controller_2_b, display3_controller_2_c, display3_controller_2_d, display3_controller_2_e,
       display3_controller_2_f, display3_controller_2_g, display3_controller_3_a, display3_controller_3_b,
       display3_controller_3_c, display3_controller_3_d, display3_controller_3_e, display3_controller_3_f,
       display3_controller_3_g, display3_controller_4_a, display3_controller_4_b, display3_controller_4_c,
       display3_controller_4_d, display3_controller_4_e, display3_controller_4_f, display3_controller_4_g,
       display4_controller_1_a, display4_controller_1_b, display4_controller_1_c, display4_controller_1_d,
       display4_controller_1_e, display4_controller_1_f, display4_controller_1_g, display4_controller_2_a,
       display4_controller_2_b, display4_controller_2_c, display4_controller_2_d, display4_controller_2_e,
       display4_controller_2_f, display4_controller_2_g, display4_controller_3_a, display4_controller_3_b,
       display4_controller_3_c, display4_controller_3_d, display4_controller_3_e, display4_controller_3_f,
       display4_controller_3_g, display4_controller_4_a, display4_controller_4_b, display4_controller_4_c,
       display4_controller_4_d, display4_controller_4_e, display4_controller_4_f, display4_controller_4_g,
       display_controller_1_a, display_controller_1_b, display_controller_1_c, display_controller_1_d,
       display_controller_1_e, display_controller_1_f, display_controller_1_g, display_controller_2_a,
       display_controller_2_b, display_controller_2_c, display_controller_2_d, display_controller_2_e,
       display_controller_2_f, display_controller_2_g, display_controller_3_a, display_controller_3_b,
       display_controller_3_c, display_controller_3_d, display_controller_3_e, display_controller_3_f,
       display_controller_3_g, display_controller_4_a, display_controller_4_b, display_controller_4_c,
       display_controller_4_d, display_controller_4_e, display_controller_4_f, display_controller_4_g,
       ex_mem_1_memread_mem, ex_mem_1_memwrite_mem, ex_mem_1_mentoreg_mem, fulldetector_1_out_6,
       fulldetector_2_out_6, fulldetector_3_out_6, fulldetector_4_out_6, Hazard, HazardLU, id_ex_1_aluop0_ex,
       id_ex_1_aluop1_id_2, id_ex_1_alusrc_ex, id_ex_1_branch_ex, id_ex_1_memread_ex, id_ex_1_memtoreg_ex,
       id_ex_1_memwrite_ex, id_ex_1_regdest_ex, Jump, mem_wb_1_memtoreg_wb, multiplexer_3_out, not_1_out,
       not_2_out, pc_counter_1_out_2, pc_counter_1_out_3, pc_counter_1_out_4, pc_counter_1_out_5,
       pc_counter_1_out_6, pc_counter_1_out_7, pc_counter_1_out_8, pc_counter_1_out_9, pc_counter_1_out_10,
       pc_counter_1_out_11, pc_counter_1_out_12, pc_counter_1_out_13, pc_counter_1_out_14,
       pc_counter_1_out_15, pc_counter_2_out_2, pc_counter_2_out_3, pc_counter_2_out_4, pc_counter_2_out_5,
       pc_counter_2_out_6, pc_counter_2_out_7, pc_counter_2_out_8, pc_counter_2_out_9, pc_counter_2_out_10,
       pc_counter_2_out_11, pc_counter_2_out_12, pc_counter_2_out_13, pc_counter_2_out_14,
       pc_counter_2_out_15, pc_counter_3_out_2, pc_counter_3_out_3, pc_counter_3_out_4, pc_counter_3_out_5,
       pc_counter_3_out_6, pc_counter_3_out_7, pc_counter_3_out_8, pc_counter_3_out_9, pc_counter_3_out_10,
       pc_counter_3_out_11, pc_counter_3_out_12, pc_counter_3_out_13, pc_counter_3_out_14,
       pc_counter_3_out_15, pc_counter_4_out_2, pc_counter_4_out_3, pc_counter_4_out_4, pc_counter_4_out_5,
       pc_counter_4_out_6, pc_counter_4_out_7, pc_counter_4_out_8, pc_counter_4_out_9, pc_counter_4_out_10,
       pc_counter_4_out_11, pc_counter_4_out_12, pc_counter_4_out_13, pc_counter_4_out_14,
       pc_counter_4_out_15, RegWrite_EX, RegWrite_ID, RegWrite_MEM, RegWrite_WB, Reset, Zero;
  wire [1:0] unit_1_forwarda, unit_1_forwardb;
  wire [4:0] Rd_EX, Rd_ID, Rd_IF, Rd_MEM, Rd_WB, Rs_EX, Rs_ID, Rs_IF, Rs_MEM, Rt_EX, Rt_ID, Rt_IF, Rt_MEM,
       Rt_WB, Rw_Ex, Rw_MEM, Rw_WB, spliter_2_shamt;
  wire [5:0] Funt_EX, Funt_ID, Funt_MEM, Funt_WB, Op_EX, Op_ID, Op_IF, Op_MEM, Op_WB;
  wire [7:0] adder_1_out, ex_mem_1_pc_mem, if_id_1_pc_if;
  wire [15:0] adder_1_out_2, ex_mem_1_pc_mem_2, if_id_1_pc_if_2, Imm16, spliter_2_offset;
  wire [23:0] adder_2_out, bit_extender_1_out, counter_1_q, id_ex_1_pc_ex, multiplexer_1_out,
       multiplexer_2_out, multiplexer_4_out, multiplexer_5_out, subtractor_1_out;
  wire [25:0] JAddress, spliter_2_address;
  wire [31:0] alu_1_resultado, ALUResult_MEM, bit_extender_2_out, BusA_EX, BusB_EX, BusW_WB,
       controlled_buffer_1_out, ex_mem_1_busb_mem, FW_A, FW_B, if_id_1_inst_id, mem_wb_1_aluresult_wb,
       mem_wb_1_busw_wb, multiplexer_6_out, multiplexer_8_out, ram_1_data, registers_1_busa, registers_1_busb;

  display_controller display_controller_1 (
    .Op5(Op_ID[5]), .Op4(Op_ID[4]), .Op3(Op_ID[3]), .Op2(Op_ID[2]), .Op1(Op_ID[1]), .Op0(Op_ID[0]),
    .Func5(Funt_ID[5]), .Func4(Funt_ID[4]), .Func3(Funt_ID[3]), .Func2(Funt_ID[2]), .Func1(Funt_ID[1]),
    .Func0(Funt_ID[0]), .a(display_controller_1_a), .b(display_controller_1_b), .c(display_controller_1_c),
    .d(display_controller_1_d), .e(display_controller_1_e), .f(display_controller_1_f),
    .g(display_controller_1_g));
  display2_controller display2_controller_1 (
    .Op5(Op_ID[5]), .Op4(Op_ID[4]), .Op3(Op_ID[3]), .Op2(Op_ID[2]), .Op1(Op_ID[1]), .Op0(Op_ID[0]),
    .Func5(Funt_ID[5]), .Func4(Funt_ID[4]), .Func3(Funt_ID[3]), .Func2(Funt_ID[2]), .Func1(Funt_ID[1]),
    .Func0(Funt_ID[0]), .a(display2_controller_1_a), .b(display2_controller_1_b),
    .c(display2_controller_1_c), .d(display2_controller_1_d), .e(display2_controller_1_e),
    .f(display2_controller_1_f), .g(display2_controller_1_g));
  display3_controller display3_controller_1 (
    .Op5(Op_ID[5]), .Op4(Op_ID[4]), .Op3(Op_ID[3]), .Op2(Op_ID[2]), .Op1(Op_ID[1]), .Op0(Op_ID[0]),
    .Func5(Funt_ID[5]), .Func4(Funt_ID[4]), .Func3(Funt_ID[3]), .Func2(Funt_ID[2]), .Func1(Funt_ID[1]),
    .Func0(Funt_ID[0]), .a(display3_controller_1_a), .b(display3_controller_1_b),
    .c(display3_controller_1_c), .d(display3_controller_1_d), .e(display3_controller_1_e),
    .f(display3_controller_1_f), .g(display3_controller_1_g));
  display4_controller display4_controller_1 (
    .Op5(Op_ID[5]), .Op4(Op_ID[4]), .Op3(Op_ID[3]), .Op2(Op_ID[2]), .Op1(Op_ID[1]), .Op0(Op_ID[0]),
    .Func5(Funt_ID[5]), .Func4(Funt_ID[4]), .Func3(Funt_ID[3]), .Func2(Funt_ID[2]), .Func1(Funt_ID[1]),
    .Func0(Funt_ID[0]), .a(display4_controller_1_a), .b(display4_controller_1_b),
    .c(display4_controller_1_c), .d(display4_controller_1_d), .e(display4_controller_1_e),
    .f(display4_controller_1_f), .g(display4_controller_1_g));
  Clock clock_1 (.out(Clock));
  Button button_1 (.out(Reset));
  _7_Segment_Display u_7_segment_display_1 (
    .g(display_controller_1_g), .f(display_controller_1_f), .a(display_controller_1_a),
    .b(display_controller_1_b), .e(display_controller_1_e), .d(display_controller_1_d),
    .c(display_controller_1_c));  // open: dp
  Multiplexer #(.width(24), .enable("false")) multiplexer_1 (
    .in0(multiplexer_5_out), .in1(JAddress[23:0]), .out(multiplexer_1_out), .sel(Jump));
  _7_Segment_Display u_7_segment_display_2 (
    .g(display2_controller_1_g), .f(display2_controller_1_f), .a(display2_controller_1_a),
    .b(display2_controller_1_b), .e(display2_controller_1_e), .d(display2_controller_1_d),
    .c(display2_controller_1_c));  // open: dp
  Counter #(.width(24), .max('hffffff)) counter_1 (
    .load(1'b1), .D(multiplexer_1_out), .count(1'b0), .Q(counter_1_q), .clk(Clock), .clr(Reset));  // open: carry
  Multiplexer #(.width(24), .enable("false")) multiplexer_2 (
    .in0(24'h1), .in1({24{1'b0}}), .out(multiplexer_2_out), .sel(HazardLU));
  _7_Segment_Display u_7_segment_display_3 (
    .g(display3_controller_1_g), .f(display3_controller_1_f), .a(display3_controller_1_a),
    .b(display3_controller_1_b), .e(display3_controller_1_e), .d(display3_controller_1_d),
    .c(display3_controller_1_c));  // open: dp
  assign bit_extender_1_out = {{9{1'b0}}, Imm16[14:0]};  // Bit_Extender bit_extender_1
  FullDetector fulldetector_1 (
    .Rd(Rd_ID), .Rs_1(Rs_IF), .RegWrite(RegWrite_ID), .Rt_1(Rt_IF), .out_6(fulldetector_1_out_6), .Rt(Rt_ID));
  _7_Segment_Display u_7_segment_display_4 (
    .g(display4_controller_1_g), .f(display4_controller_1_f), .a(display4_controller_1_a),
    .b(display4_controller_1_b), .e(display4_controller_1_e), .d(display4_controller_1_d),
    .c(display4_controller_1_c));  // open: dp
  RAM #(.addrWidth(24), .dataWidth(32)) ram_1 (.addr(counter_1_q), .data(ram_1_data));  // open: sel, clk, ld, clr
  Adder #(.width(24)) adder_1 (
    .a(counter_1_q), .b(multiplexer_2_out), .out({adder_1_out_2, adder_1_out}));  // open: cin, cout
  Adder #(.width(24)) adder_2 (
    .a({adder_1_out_2, adder_1_out}), .b(bit_extender_1_out), .out(adder_2_out));  // open: cin, cout
  Subtractor #(.width(24)) subtractor_1 (
    .a({adder_1_out_2, adder_1_out}), .b(bit_extender_1_out), .out(subtractor_1_out));  // open: bin, bout
  Multiplexer #(.enable("false")) multiplexer_3 (.in0(Zero), .in1(not_1_out), .out(multiplexer_3_out), .sel(bne));
  LED led_1 (.in(fulldetector_1_out_6));
  _7_Segment_Display u_7_segment_display_5 (
    .g(pc_counter_1_out_8), .f(pc_counter_1_out_7), .a(pc_counter_1_out_2), .b(pc_counter_1_out_3),
    .e(pc_counter_1_out_6), .d(pc_counter_1_out_5), .c(pc_counter_1_out_4));  // open: dp
  Multiplexer #(.width(24), .enable("false")) multiplexer_4 (
    .in0(adder_2_out), .in1(subtractor_1_out), .out(multiplexer_4_out), .sel(Imm16[15]));
  and and_1 (and_1_out, multiplexer_3_out, Branch);
  not not_1 (not_1_out, Zero);
  pc_counter pc_counter_1 (
    .out_2(pc_counter_1_out_2), .out_3(pc_counter_1_out_3), .out_4(pc_counter_1_out_4),
    .out_5(pc_counter_1_out_5), .out_6(pc_counter_1_out_6), .out_7(pc_counter_1_out_7),
    .out_8(pc_counter_1_out_8), .out_9(pc_counter_1_out_9), .out_10(pc_counter_1_out_10),
    .out_11(pc_counter_1_out_11), .out_12(pc_counter_1_out_12), .out_13(pc_counter_1_out_13),
    .out_14(pc_counter_1_out_14), .out_15(pc_counter_1_out_15), .in_1(adder_1_out));
  spliter spliter_1 (
    .in_1(ram_1_data), .rd(Rd_IF), .rt(Rt_IF), .rs(Rs_IF), .op(Op_IF));  // open: funct, shamt, address, offset
  Multiplexer #(.width(24), .enable("false")) multiplexer_5 (
    .in0({adder_1_out_2, adder_1_out}), .in1(multiplexer_4_out), .out(multiplexer_5_out), .sel(and_1_out));
  Multiplexer #(.width(32), .enable("false")) multiplexer_6 (
    .in0(ram_1_data), .in1({32{1'b0}}), .out(multiplexer_6_out), .sel(HazardLU));
  FullDetector fulldetector_2 (
    .Rd(Rw_Ex), .Rs_1(Rs_IF), .RegWrite(RegWrite_EX), .Rt_1(Rt_IF), .out_6(fulldetector_2_out_6), .Rt(Rt_EX));
  LED led_2 (.in(fulldetector_2_out_6));
  IF_ID if_id_1 (
    .Inst_IF(multiplexer_6_out), .Clock(Clock), .PC_ID({adder_1_out_2, adder_1_out}),
    .Inst_ID(if_id_1_inst_id), .Clear(Reset), .PC_IF({if_id_1_pc_if_2, if_id_1_pc_if}), .Enable(1'b1));
  _7_Segment_Display u_7_segment_display_6 (
    .g(pc_counter_1_out_15), .f(pc_counter_1_out_14), .a(pc_counter_1_out_9), .b(pc_counter_1_out_10),
    .e(pc_counter_1_out_13), .d(pc_counter_1_out_12), .c(pc_counter_1_out_11));  // open: dp
  spliter spliter_2 (
    .in_1(if_id_1_inst_id), .funct(Funt_ID), .shamt(spliter_2_shamt), .rd(Rd_ID), .rt(Rt_ID), .rs(Rs_ID),
    .op(Op_ID), .address(spliter_2_address), .offset(spliter_2_offset));
  control control_1 (
    .Jump(control_1_jump), .OPCODE(Op_ID), .RegDst(control_1_regdst), .ALUSrc(control_1_alusrc),
    .MemtoReg(control_1_memtoreg), .RegWrite(control_1_regwrite), .MemRead(control_1_memread),
    .MemWrite(control_1_memwrite), .Branch(control_1_branch), .ALUOp1(control_1_aluop1),
    .ALUOp0(control_1_aluop0), .bne(control_1_bne));
  or or_1 (Hazard, fulldetector_1_out_6, fulldetector_2_out_6, fulldetector_3_out_6, fulldetector_4_out_6);
  Comparator #(.width(32)) comparator_1 (.a(if_id_1_inst_id), .b({32{1'b0}}), .eq(comparator_1_eq));  // open: gt, lt
  FullDetector fulldetector_3 (
    .Rd(Rw_MEM), .Rs_1(Rs_IF), .RegWrite(RegWrite_MEM), .Rt_1(Rt_IF), .out_6(fulldetector_3_out_6),
    .Rt(Rt_MEM));
  _7_Segment_Display u_7_segment_display_7 (
    .g(pc_counter_2_out_8), .f(pc_counter_2_out_7), .a(pc_counter_2_out_2), .b(pc_counter_2_out_3),
    .e(pc_counter_2_out_6), .d(pc_counter_2_out_5), .c(pc_counter_2_out_4));  // open: dp
  Multiplexer #(.enable("false")) multiplexer_7 (
    .in0(control_1_regwrite), .in1(1'b0), .out(RegWrite_ID), .sel(comparator_1_eq));
  LED led_3 (.in(fulldetector_3_out_6));
  pc_counter pc_counter_2 (
    .out_2(pc_counter_2_out_2), .out_3(pc_counter_2_out_3), .out_4(pc_counter_2_out_4),
    .out_5(pc_counter_2_out_5), .out_6(pc_counter_2_out_6), .out_7(pc_counter_2_out_7),
    .out_8(pc_counter_2_out_8), .out_9(pc_counter_2_out_9), .out_10(pc_counter_2_out_10),
    .out_11(pc_counter_2_out_11), .out_12(pc_counter_2_out_12), .out_13(pc_counter_2_out_13),
    .out_14(pc_counter_2_out_14), .out_15(pc_counter_2_out_15), .in_1(if_id_1_pc_if));
  registers registers_1 (
    .busW(BusW_WB), .Reset(Reset), .Clock(Clock), .busA(registers_1_busa), .busB(registers_1_busb),
    .Enable_RegWr(RegWrite_WB), .Rw(Rw_WB), .Ra(Rs_ID), .Rb(Rt_ID));
  display_controller display_controller_2 (
    .Op5(Op_EX[5]), .Op4(Op_EX[4]), .Op3(Op_EX[3]), .Op2(Op_EX[2]), .Op1(Op_EX[1]), .Op0(Op_EX[0]),
    .Func5(Funt_EX[5]), .Func4(Funt_EX[4]), .Func3(Funt_EX[3]), .Func2(Funt_EX[2]), .Func1(Funt_EX[1]),
    .Func0(Funt_EX[0]), .a(display_controller_2_a), .b(display_controller_2_b), .c(display_controller_2_c),
    .d(display_controller_2_d), .e(display_controller_2_e), .f(display_controller_2_f),
    .g(display_controller_2_g));
  display2_controller display2_controller_2 (
    .Op5(Op_EX[5]), .Op4(Op_EX[4]), .Op3(Op_EX[3]), .Op2(Op_EX[2]), .Op1(Op_EX[1]), .Op0(Op_EX[0]),
    .Func5(Funt_EX[5]), .Func4(Funt_EX[4]), .Func3(Funt_EX[3]), .Func2(Funt_EX[2]), .Func1(Funt_EX[1]),
    .Func0(Funt_EX[0]), .a(display2_controller_2_a), .b(display2_controller_2_b),
    .c(display2_controller_2_c), .d(display2_controller_2_d), .e(display2_controller_2_e),
    .f(display2_controller_2_f), .g(display2_controller_2_g));
  display3_controller display3_controller_2 (
    .Op5(Op_EX[5]), .Op4(Op_EX[4]), .Op3(Op_EX[3]), .Op2(Op_EX[2]), .Op1(Op_EX[1]), .Op0(Op_EX[0]),
    .Func5(Funt_EX[5]), .Func4(Funt_EX[4]), .Func3(Funt_EX[3]), .Func2(Funt_EX[2]), .Func1(Funt_EX[1]),
    .Func0(Funt_EX[0]), .a(display3_controller_2_a), .b(display3_controller_2_b),
    .c(display3_controller_2_c), .d(display3_controller_2_d), .e(display3_controller_2_e),
    .f(display3_controller_2_f), .g(display3_controller_2_g));
  display4_controller display4_controller_2 (
    .Op5(Op_EX[5]), .Op4(Op_EX[4]), .Op3(Op_EX[3]), .Op2(Op_EX[2]), .Op1(Op_EX[1]), .Op0(Op_EX[0]),
    .Func5(Funt_EX[5]), .Func4(Funt_EX[4]), .Func3(Funt_EX[3]), .Func2(Funt_EX[2]), .Func1(Funt_EX[1]),
    .Func0(Funt_EX[0]), .a(display4_controller_2_a), .b(display4_controller_2_b),
    .c(display4_controller_2_c), .d(display4_controller_2_d), .e(display4_controller_2_e),
    .f(display4_controller_2_f), .g(display4_controller_2_g));
  _7_Segment_Display u_7_segment_display_8 (
    .g(display_controller_2_g), .f(display_controller_2_f), .a(display_controller_2_a),
    .b(display_controller_2_b), .e(display_controller_2_e), .d(display_controller_2_d),
    .c(display_controller_2_c));  // open: dp
  FullDetector fulldetector_4 (
    .Rd(Rw_WB), .Rs_1(Rs_IF), .RegWrite(RegWrite_WB), .Rt_1(Rt_IF), .out_6(fulldetector_4_out_6), .Rt(Rt_WB));
  _7_Segment_Display u_7_segment_display_9 (
    .g(display2_controller_2_g), .f(display2_controller_2_f), .a(display2_controller_2_a),
    .b(display2_controller_2_b), .e(display2_controller_2_e), .d(display2_controller_2_d),
    .c(display2_controller_2_c));  // open: dp
  _7_Segment_Display u_7_segment_display_10 (
    .g(pc_counter_2_out_15), .f(pc_counter_2_out_14), .a(pc_counter_2_out_9), .b(pc_counter_2_out_10),
    .e(pc_counter_2_out_13), .d(pc_counter_2_out_12), .c(pc_counter_2_out_11));  // open: dp
  ID_EX id_ex_1 (
    .Imm_ID(spliter_2_offset), .Shamt_ID(spliter_2_shamt), .ALUSrc_ID(control_1_alusrc),
    .MemtoReg_ID(control_1_memtoreg), .Clock(Clock), .RegWrite_ID(RegWrite_ID),
    .PC_ID({if_id_1_pc_if_2, if_id_1_pc_if}), .Jump_ID(control_1_jump), .MemRead_ID(control_1_memread),
    .MemWrite_ID(control_1_memwrite), .Branch_ID(control_1_branch), .Bne_ID(control_1_bne), .Imm_EX(Imm16),
    .Shamt_EX(out_1), .ALUSrc_EX(id_ex_1_alusrc_ex), .MemtoReg_EX(id_ex_1_memtoreg_ex),
    .RegWrite_EX(RegWrite_EX), .PC_EX(id_ex_1_pc_ex), .Jump_EX(Jump), .MemRead_EX(id_ex_1_memread_ex),
    .MemWrite_EX(id_ex_1_memwrite_ex), .Branch_EX(id_ex_1_branch_ex), .Bne_EX(bne), .Clear(Reset),
    .Enable(1'b1), .BusB_EX(BusB_EX), .BusB_ID(registers_1_busb), .BusA_EX(BusA_EX),
    .BusA_ID(registers_1_busa), .JumpAddr_2(JAddress), .JumpAddr(spliter_2_address), .Rd_ID(Rd_ID),
    .Rd_EX(Rd_EX), .Rt_ID(Rt_ID), .Rt_EX(Rt_EX), .Rs_ID(Rs_ID), .Rs_EX(Rs_EX), .RegDest_ID(control_1_regdst),
    .RegDest_EX(id_ex_1_regdest_ex), .ALUOP0_ID(control_1_aluop0), .ALUOP0_EX(id_ex_1_aluop0_ex),
    .ALUOP1_ID(control_1_aluop1), .ALUOP1_ID_2(id_ex_1_aluop1_id_2), .Funct_ID(Funt_ID), .Funct_EX(Funt_EX),
    .Op_ID(Op_ID), .Op_EX(Op_EX));  // open: ALUCtrl3_ID, ALUCtrl2_ID, ALUCtrl1_ID, ALUCtrl0_ID, ALUCtrl3_EX, ALUCtrl2_EX, ALUCtrl1_EX, ALUCtrl0_EX
  LED led_4 (.in(fulldetector_4_out_6));
  _7_Segment_Display u_7_segment_display_11 (
    .g(pc_counter_3_out_8), .f(pc_counter_3_out_7), .a(pc_counter_3_out_2), .b(pc_counter_3_out_3),
    .e(pc_counter_3_out_6), .d(pc_counter_3_out_5), .c(pc_counter_3_out_4));  // open: dp
  pc_counter pc_counter_3 (
    .out_2(pc_counter_3_out_2), .out_3(pc_counter_3_out_3), .out_4(pc_counter_3_out_4),
    .out_5(pc_counter_3_out_5), .out_6(pc_counter_3_out_6), .out_7(pc_counter_3_out_7),
    .out_8(pc_counter_3_out_8), .out_9(pc_counter_3_out_9), .out_10(pc_counter_3_out_10),
    .out_11(pc_counter_3_out_11), .out_12(pc_counter_3_out_12), .out_13(pc_counter_3_out_13),
    .out_14(pc_counter_3_out_14), .out_15(pc_counter_3_out_15), .in_1(id_ex_1_pc_ex[7:0]));
  assign bit_extender_2_out = {{16{1'b0}}, Imm16};  // Bit_Extender bit_extender_2
  _7_Segment_Display u_7_segment_display_12 (
    .g(display3_controller_2_g), .f(display3_controller_2_f), .a(display3_controller_2_a),
    .b(display3_controller_2_b), .e(display3_controller_2_e), .d(display3_controller_2_d),
    .c(display3_controller_2_c));  // open: dp
  ALUControl alucontrol_1 (
    .ALUOp1(id_ex_1_aluop1_id_2), .ALUOp0(id_ex_1_aluop0_ex), .F5(Funt_EX[5]), .F4(Funt_EX[4]),
    .F3(Funt_EX[3]), .F2(Funt_EX[2]), .F1(Funt_EX[1]), .F0(Funt_EX[0]), .ALUCtrl3(alucontrol_1_aluctrl3),
    .ALUCtrl2(alucontrol_1_aluctrl2), .ALUCtrl1(alucontrol_1_aluctrl1), .ALUCtrl0(alucontrol_1_aluctrl0));
  Multiplexer #(.width(32), .enable("false")) multiplexer_8 (
    .in0(FW_B), .in1(bit_extender_2_out), .out(multiplexer_8_out), .sel(id_ex_1_alusrc_ex));
  _7_Segment_Display u_7_segment_display_13 (
    .g(display4_controller_2_g), .f(display4_controller_2_f), .a(display4_controller_2_a),
    .b(display4_controller_2_b), .e(display4_controller_2_e), .d(display4_controller_2_d),
    .c(display4_controller_2_c));  // open: dp
  Multiplexer #(.width(5), .disabled(0), .enable("false")) multiplexer_9 (
    .in0(Rt_EX), .in1(Rd_EX), .out(Rw_Ex), .sel(id_ex_1_regdest_ex));
  ALU alu_1 (
    .in_5(FW_A), .in_6(multiplexer_8_out), .ALUCtrl3(alucontrol_1_aluctrl3),
    .ALUCtrl2(alucontrol_1_aluctrl2), .ALUCtrl1(alucontrol_1_aluctrl1), .ALUCtrl0(alucontrol_1_aluctrl0),
    .Resultado(alu_1_resultado), .out_8(alu_1_out_8));
  _7_Segment_Display u_7_segment_display_14 (
    .g(pc_counter_3_out_15), .f(pc_counter_3_out_14), .a(pc_counter_3_out_9), .b(pc_counter_3_out_10),
    .e(pc_counter_3_out_13), .d(pc_counter_3_out_12), .c(pc_counter_3_out_11));  // open: dp
  // Probe on FW_A
  Multiplexer #(.select(2), .width(32), .enable("false")) multiplexer_10 (
    .in0(BusA_EX), .in1(BusW_WB), .in2(ALUResult_MEM), .out(FW_A), .sel(unit_1_forwarda));  // open: in3
  // Probe on unit_1_forwarda
  _7_Segment_Display u_7_segment_display_15 (
    .g(pc_counter_4_out_8), .f(pc_counter_4_out_7), .a(pc_counter_4_out_2), .b(pc_counter_4_out_3),
    .e(pc_counter_4_out_6), .d(pc_counter_4_out_5), .c(pc_counter_4_out_4));  // open: dp
  EX_MEM ex_mem_1 (
    .MentoReg_EX(id_ex_1_memtoreg_ex), .ALUResult_EX(alu_1_resultado), .RegWrite_EX(RegWrite_EX),
    .MemRead_EX(id_ex_1_memread_ex), .PC_EX(id_ex_1_pc_ex), .MemWrite_EX(id_ex_1_memwrite_ex),
    .MentoReg_MEM(ex_mem_1_mentoreg_mem), .ALUResult_MEM(ALUResult_MEM), .RegWrite_MEM(RegWrite_MEM),
    .MemRead_MEM(ex_mem_1_memread_mem), .PC_MEM({ex_mem_1_pc_mem_2, ex_mem_1_pc_mem}),
    .MemWrite_MEM(ex_mem_1_memwrite_mem), .Clock(Clock), .Clear(Reset), .Enable(1'b1), .BusB_EX(FW_B),
    .BusB_MEM(ex_mem_1_busb_mem), .Rd_EX(Rd_EX), .Rd_MEM(Rd_MEM), .Rt_EX(Rt_EX), .Rt_MEM(Rt_MEM),
    .Rs_EX(Rs_EX), .Rs_MEM(Rs_MEM), .Funct_EX(Funt_EX), .Funct_MEM(Funt_MEM), .RW_EX(Rw_Ex), .RW_MEM(Rw_MEM),
    .Zero_EX(alu_1_out_8), .Zero_MEM(Zero), .Branch_EX(id_ex_1_branch_ex), .Branch_MEM(Branch),
    .Op_EX(Op_EX), .Op_MEM(Op_MEM));  // open: RegDest_EX, RegDest_MEM, ALUOP0_EX, ALUOP0_MEM, ALUOP1_EX, ALUOP1_MEM
  // Probe on BusA_EX
  pc_counter pc_counter_4 (
    .out_2(pc_counter_4_out_2), .out_3(pc_counter_4_out_3), .out_4(pc_counter_4_out_4),
    .out_5(pc_counter_4_out_5), .out_6(pc_counter_4_out_6), .out_7(pc_counter_4_out_7),
    .out_8(pc_counter_4_out_8), .out_9(pc_counter_4_out_9), .out_10(pc_counter_4_out_10),
    .out_11(pc_counter_4_out_11), .out_12(pc_counter_4_out_12), .out_13(pc_counter_4_out_13),
    .out_14(pc_counter_4_out_14), .out_15(pc_counter_4_out_15), .in_1(ex_mem_1_pc_mem));
  assign controlled_buffer_1_out = ex_mem_1_memwrite_mem ? ex_mem_1_busb_mem : 32'bz;  // Controlled_Buffer controlled_buffer_1
  not not_2 (not_2_out, ex_mem_1_memwrite_mem);
  Unit unit_1 (
    .EX_MEM_RegWrite(RegWrite_MEM), .EX_MEM_RegisterRd(Rw_MEM), .ID_EX_RegisterRs(Rs_EX),
    .ID_EX_RegisterRt(Rt_EX), .MEM_WB_RegWrite(RegWrite_WB), .MEM_WB_RegisterRd(Rw_WB),
    .ForwardA(unit_1_forwarda), .ForwardB(unit_1_forwardb));
  RAM #(.addrWidth(24), .dataWidth(32)) ram_2 (
    .addr(ALUResult_MEM[23:0]), .data(controlled_buffer_1_out), .clk(Clock), .ld(not_2_out), .clr(Reset));  // open: sel
  _7_Segment_Display u_7_segment_display_16 (
    .g(pc_counter_4_out_15), .f(pc_counter_4_out_14), .a(pc_counter_4_out_9), .b(pc_counter_4_out_10),
    .e(pc_counter_4_out_13), .d(pc_counter_4_out_12), .c(pc_counter_4_out_11));  // open: dp
  Multiplexer #(.select(2), .width(32), .enable("false")) multiplexer_11 (
    .in0(BusB_EX), .in1(BusW_WB), .in2(ALUResult_MEM), .out(FW_B), .sel(unit_1_forwardb));  // open: in3
  // Probe on unit_1_forwardb
  MEM_WB mem_wb_1 (
    .ALUResult_MEM(ALUResult_MEM), .MemtoReg_MEM(ex_mem_1_mentoreg_mem), .RegWriteMEM(RegWrite_MEM),
    .BusW_MEM(controlled_buffer_1_out), .PC_MEM({ex_mem_1_pc_mem_2, ex_mem_1_pc_mem}),
    .ALUResult_WB(mem_wb_1_aluresult_wb), .MemtoReg_WB(mem_wb_1_memtoreg_wb), .RegWriteWB(RegWrite_WB),
    .BusW_WB(mem_wb_1_busw_wb), .Clock(Clock), .Clear(Reset), .Enable(1'b1), .Rd_MEM(Rd_MEM), .Rd_WB(Rd_WB),
    .Rt_MEM(Rt_MEM), .Rt_WB(Rt_WB), .Rs_MEM(Rs_MEM), .Funct_MEM(Funt_MEM), .Funct_WB(Funt_WB),
    .RW_MEM(Rw_MEM), .RW_WB(Rw_WB), .OP_MEM(Op_MEM), .OP_WB(Op_WB));  // open: MemRead_MEM, MemRead_WB, PC_WB, Rs_WB, RegDest_MEM, RegDest_WB, ALUOP0_MEM, ALUOP0_WB, ALUOP1_MEM, ALUOP1_WB
  Multiplexer #(.width(32), .enable("false")) multiplexer_12 (
    .in0(mem_wb_1_aluresult_wb), .in1(mem_wb_1_busw_wb), .out(BusW_WB), .sel(mem_wb_1_memtoreg_wb));
  display_controller display_controller_3 (
    .Op5(Op_MEM[5]), .Op4(Op_MEM[4]), .Op3(Op_MEM[3]), .Op2(Op_MEM[2]), .Op1(Op_MEM[1]), .Op0(Op_MEM[0]),
    .Func5(Funt_MEM[5]), .Func4(Funt_MEM[4]), .Func3(Funt_MEM[3]), .Func2(Funt_MEM[2]), .Func1(Funt_MEM[1]),
    .Func0(Funt_MEM[0]), .a(display_controller_3_a), .b(display_controller_3_b), .c(display_controller_3_c),
    .d(display_controller_3_d), .e(display_controller_3_e), .f(display_controller_3_f),
    .g(display_controller_3_g));
  display2_controller display2_controller_3 (
    .Op5(Op_MEM[5]), .Op4(Op_MEM[4]), .Op3(Op_MEM[3]), .Op2(Op_MEM[2]), .Op1(Op_MEM[1]), .Op0(Op_MEM[0]),
    .Func5(Funt_MEM[5]), .Func4(Funt_MEM[4]), .Func3(Funt_MEM[3]), .Func2(Funt_MEM[2]), .Func1(Funt_MEM[1]),
    .Func0(Funt_MEM[0]), .a(display2_controller_3_a), .b(display2_controller_3_b),
    .c(display2_controller_3_c), .d(display2_controller_3_d), .e(display2_controller_3_e),
    .f(display2_controller_3_f), .g(display2_controller_3_g));
  display3_controller display3_controller_3 (
    .Op5(Op_MEM[5]), .Op4(Op_MEM[4]), .Op3(Op_MEM[3]), .Op2(Op_MEM[2]), .Op1(Op_MEM[1]), .Op0(Op_MEM[0]),
    .Func5(Funt_MEM[5]), .Func4(Funt_MEM[4]), .Func3(Funt_MEM[3]), .Func2(Funt_MEM[2]), .Func1(Funt_MEM[1]),
    .Func0(Funt_MEM[0]), .a(display3_controller_3_a), .b(display3_controller_3_b),
    .c(display3_controller_3_c), .d(display3_controller_3_d), .e(display3_controller_3_e),
    .f(display3_controller_3_f), .g(display3_controller_3_g));
  display4_controller display4_controller_3 (
    .Op5(Op_MEM[5]), .Op4(Op_MEM[4]), .Op3(Op_MEM[3]), .Op2(Op_MEM[2]), .Op1(Op_MEM[1]), .Op0(Op_MEM[0]),
    .Func5(Funt_MEM[5]), .Func4(Funt_MEM[4]), .Func3(Funt_MEM[3]), .Func2(Funt_MEM[2]), .Func1(Funt_MEM[1]),
    .Func0(Funt_MEM[0]), .a(display4_controller_3_a), .b(display4_controller_3_b),
    .c(display4_controller_3_c), .d(display4_controller_3_d), .e(display4_controller_3_e),
    .f(display4_controller_3_f), .g(display4_controller_3_g));
  _7_Segment_Display u_7_segment_display_17 (
    .g(display_controller_3_g), .f(display_controller_3_f), .a(display_controller_3_a),
    .b(display_controller_3_b), .e(display_controller_3_e), .d(display_controller_3_d),
    .c(display_controller_3_c));  // open: dp
  Load_use load_use_1 (
    .ID_EX_MemRead(RegWrite_ID), .ID_EX_RegisterRt(Rt_ID), .IF_ID_RegisterRS(Rs_IF),
    .IF_ID_RegisterRt(Rt_IF), .Hazard(HazardLU), .ID_EX_RegisterRd(Rd_ID));
  LED led_5 (.in(HazardLU));
  _7_Segment_Display u_7_segment_display_18 (
    .g(display2_controller_3_g), .f(display2_controller_3_f), .a(display2_controller_3_a),
    .b(display2_controller_3_b), .e(display2_controller_3_e), .d(display2_controller_3_d),
    .c(display2_controller_3_c));  // open: dp
  _7_Segment_Display u_7_segment_display_19 (
    .g(display3_controller_3_g), .f(display3_controller_3_f), .a(display3_controller_3_a),
    .b(display3_controller_3_b), .e(display3_controller_3_e), .d(display3_controller_3_d),
    .c(display3_controller_3_c));  // open: dp
  _7_Segment_Display u_7_segment_display_20 (
    .g(display4_controller_3_g), .f(display4_controller_3_f), .a(display4_controller_3_a),
    .b(display4_controller_3_b), .e(display4_controller_3_e), .d(display4_controller_3_d),
    .c(display4_controller_3_c));  // open: dp
  display_controller display_controller_4 (
    .Op5(Op_WB[5]), .Op4(Op_WB[4]), .Op3(Op_WB[3]), .Op2(Op_WB[2]), .Op1(Op_WB[1]), .Op0(Op_WB[0]),
    .Func5(Funt_WB[5]), .Func4(Funt_WB[4]), .Func3(Funt_WB[3]), .Func2(Funt_WB[2]), .Func1(Funt_WB[1]),
    .Func0(Funt_WB[0]), .a(display_controller_4_a), .b(display_controller_4_b), .c(display_controller_4_c),
    .d(display_controller_4_d), .e(display_controller_4_e), .f(display_controller_4_f),
    .g(display_controller_4_g));
  display2_controller display2_controller_4 (
    .Op5(Op_WB[5]), .Op4(Op_WB[4]), .Op3(Op_WB[3]), .Op2(Op_WB[2]), .Op1(Op_WB[1]), .Op0(Op_WB[0]),
    .Func5(Funt_WB[5]), .Func4(Funt_WB[4]), .Func3(Funt_WB[3]), .Func2(Funt_WB[2]), .Func1(Funt_WB[1]),
    .Func0(Funt_WB[0]), .a(display2_controller_4_a), .b(display2_controller_4_b),
    .c(display2_controller_4_c), .d(display2_controller_4_d), .e(display2_controller_4_e),
    .f(display2_controller_4_f), .g(display2_controller_4_g));
  display3_controller display3_controller_4 (
    .Op5(Op_WB[5]), .Op4(Op_WB[4]), .Op3(Op_WB[3]), .Op2(Op_WB[2]), .Op1(Op_WB[1]), .Op0(Op_WB[0]),
    .Func5(Funt_WB[5]), .Func4(Funt_WB[4]), .Func3(Funt_WB[3]), .Func2(Funt_WB[2]), .Func1(Funt_WB[1]),
    .Func0(Funt_WB[0]), .a(display3_controller_4_a), .b(display3_controller_4_b),
    .c(display3_controller_4_c), .d(display3_controller_4_d), .e(display3_controller_4_e),
    .f(display3_controller_4_f), .g(display3_controller_4_g));
  display4_controller display4_controller_4 (
    .Op5(Op_WB[5]), .Op4(Op_WB[4]), .Op3(Op_WB[3]), .Op2(Op_WB[2]), .Op1(Op_WB[1]), .Op0(Op_WB[0]),
    .Func5(Funt_WB[5]), .Func4(Funt_WB[4]), .Func3(Funt_WB[3]), .Func2(Funt_WB[2]), .Func1(Funt_WB[1]),
    .Func0(Funt_WB[0]), .a(display4_controller_4_a), .b(display4_controller_4_b),
    .c(display4_controller_4_c), .d(display4_controller_4_d), .e(display4_controller_4_e),
    .f(display4_controller_4_f), .g(display4_controller_4_g));
  _7_Segment_Display u_7_segment_display_21 (
    .g(display_controller_4_g), .f(display_controller_4_f), .a(display_controller_4_a),
    .b(display_controller_4_b), .e(display_controller_4_e), .d(display_controller_4_d),
    .c(display_controller_4_c));  // open: dp
  _7_Segment_Display u_7_segment_display_22 (
    .g(display2_controller_4_g), .f(display2_controller_4_f), .a(display2_controller_4_a),
    .b(display2_controller_4_b), .e(display2_controller_4_e), .d(display2_controller_4_d),
    .c(display2_controller_4_c));  // open: dp
  _7_Segment_Display u_7_segment_display_23 (
    .g(display3_controller_4_g), .f(display3_controller_4_f), .a(display3_controller_4_a),
    .b(display3_controller_4_b), .e(display3_controller_4_e), .d(display3_controller_4_d),
    .c(display3_controller_4_c));  // open: dp
  _7_Segment_Display u_7_segment_display_24 (
    .g(display4_controller_4_g), .f(display4_controller_4_f), .a(display4_controller_4_a),
    .b(display4_controller_4_b), .e(display4_controller_4_e), .d(display4_controller_4_d),
    .c(display4_controller_4_c));  // open: dp

  // Notes on the sheet:
  //   Hazard detector IF - ID
  //   ID INST
  //   PC
  //   Hazard detector IF - EX
  //   BusW
  //   Hazard detector IF - MEM
  //   PC
  //   Registros
  //   BusA
  //   BusB
  //   Hazard detector IF - WB
  //   EX INST
  //   ALUSrc
  //   PC
  //   BusB
  //   BusW / WriteBack
  //   RW
  //   ALU
  //   Entrada 1 ALU
  //   RW
  //   RegWrite
  //   PC
  //   BusB
  //   MemRead
  //   Data Memory
  //   Entrada 2 ALU
  //   MemtoReg
  //   MEM INST
  //   WB INST
endmodule

module main_SC (
);

  wire ALUCtrl0, ALUCtrl1, ALUCtrl2, ALUCtrl3, ALUSrc, and_1_out, bne, Branch, Clock, control_1_aluop0,
       control_1_aluop1, display2_controller_1_a, display2_controller_1_b, display2_controller_1_c,
       display2_controller_1_d, display2_controller_1_e, display2_controller_1_f, display2_controller_1_g,
       display3_controller_1_a, display3_controller_1_b, display3_controller_1_c, display3_controller_1_d,
       display3_controller_1_e, display3_controller_1_f, display3_controller_1_g, display4_controller_1_a,
       display4_controller_1_b, display4_controller_1_c, display4_controller_1_d, display4_controller_1_e,
       display4_controller_1_f, display4_controller_1_g, display_controller_1_a, display_controller_1_b,
       display_controller_1_c, display_controller_1_d, display_controller_1_e, display_controller_1_f,
       display_controller_1_g, Jump, MemRead, MemtoReg, MemWrite, multiplexer_4_out, not_1_out, not_2_out,
       RegDst, RegWrite, Reset, Zero;
  wire [4:0] Rd, Rs, Rt, Rw, spliter_1_shamt;
  wire [5:0] spliter_1_funct, spliter_1_op;
  wire [15:0] Imm16;
  wire [23:0] adder_1_out, adder_2_out, alu_1_resultado, bit_extender_1_out, counter_1_q, multiplexer_1_out,
       multiplexer_2_out, multiplexer_3_out, subtractor_1_out;
  wire [25:0] JAddress;
  wire [31:0] controlled_buffer_1_out, multiplexer_6_out, multiplexer_7_out, ram_1_data, registers_1_busa,
       registers_1_busb, SExtender;
  wire [31:24] alu_1_resultado_2;

  Multiplexer #(.width(24), .enable("false")) multiplexer_1 (
    .in0(multiplexer_3_out), .in1(JAddress[23:0]), .out(multiplexer_1_out), .sel(Jump));
  Clock clock_1 (.out(Clock));
  Button button_1 (.out(Reset));
  Counter #(.width(24), .max('hffffff)) counter_1 (
    .load(1'b1), .D(multiplexer_1_out), .count(1'b0), .Q(counter_1_q), .clk(Clock), .clr(Reset));  // open: carry
  assign bit_extender_1_out = {{9{1'b0}}, Imm16[14:0]};  // Bit_Extender bit_extender_1
  Adder #(.width(24)) adder_1 (.a(counter_1_q), .b(24'h1), .out(adder_1_out));  // open: cin, cout
  RAM #(.addrWidth(24), .dataWidth(32)) ram_1 (.addr(counter_1_q), .data(ram_1_data));  // open: sel, clk, ld, clr
  Adder #(.width(24)) adder_2 (.a(adder_1_out), .b(bit_extender_1_out), .out(adder_2_out));  // open: cin, cout
  Multiplexer #(.width(24), .enable("false")) multiplexer_2 (
    .in0(adder_2_out), .in1(subtractor_1_out), .out(multiplexer_2_out), .sel(Imm16[15]));
  Subtractor #(.width(24)) subtractor_1 (
    .a(adder_1_out), .b(bit_extender_1_out), .out(subtractor_1_out));  // open: bin, bout
  // Probe on spliter_1_shamt
  spliter spliter_1 (
    .in_1(ram_1_data), .funct(spliter_1_funct), .shamt(spliter_1_shamt), .rd(Rd), .rt(Rt), .rs(Rs),
    .op(spliter_1_op), .address(JAddress), .offset(Imm16));
  Multiplexer #(.width(24), .enable("false")) multiplexer_3 (
    .in0(adder_1_out), .in1(multiplexer_2_out), .out(multiplexer_3_out), .sel(and_1_out));
  and and_1 (and_1_out, multiplexer_4_out, Branch);
  Multiplexer #(.enable("false")) multiplexer_4 (.in0(Zero), .in1(not_1_out), .out(multiplexer_4_out), .sel(bne));
  not not_1 (not_1_out, Zero);
  control control_1 (
    .Jump(Jump), .OPCODE(spliter_1_op), .RegDst(RegDst), .ALUSrc(ALUSrc), .MemtoReg(MemtoReg),
    .RegWrite(RegWrite), .MemRead(MemRead), .MemWrite(MemWrite), .Branch(Branch), .ALUOp1(control_1_aluop1),
    .ALUOp0(control_1_aluop0), .bne(bne));
  Multiplexer #(.width(5), .disabled(0), .enable("false")) multiplexer_5 (.in0(Rt), .in1(Rd), .out(Rw), .sel(RegDst));
  ALUControl alucontrol_1 (
    .ALUOp1(control_1_aluop1), .ALUOp0(control_1_aluop0), .F5(spliter_1_funct[5]), .F4(spliter_1_funct[4]),
    .F3(spliter_1_funct[3]), .F2(spliter_1_funct[2]), .F1(spliter_1_funct[1]), .F0(spliter_1_funct[0]),
    .ALUCtrl3(ALUCtrl3), .ALUCtrl2(ALUCtrl2), .ALUCtrl1(ALUCtrl1), .ALUCtrl0(ALUCtrl0));
  display_controller display_controller_1 (
    .Op5(spliter_1_op[5]), .Op4(spliter_1_op[4]), .Op3(spliter_1_op[3]), .Op2(spliter_1_op[2]),
    .Op1(spliter_1_op[1]), .Op0(spliter_1_op[0]), .Func5(spliter_1_funct[5]), .Func4(spliter_1_funct[4]),
    .Func3(spliter_1_funct[3]), .Func2(spliter_1_funct[2]), .Func1(spliter_1_funct[1]),
    .Func0(spliter_1_funct[0]), .a(display_controller_1_a), .b(display_controller_1_b),
    .c(display_controller_1_c), .d(display_controller_1_d), .e(display_controller_1_e),
    .f(display_controller_1_f), .g(display_controller_1_g));
  display2_controller display2_controller_1 (
    .Op5(spliter_1_op[5]), .Op4(spliter_1_op[4]), .Op3(spliter_1_op[3]), .Op2(spliter_1_op[2]),
    .Op1(spliter_1_op[1]), .Op0(spliter_1_op[0]), .Func5(spliter_1_funct[5]), .Func4(spliter_1_funct[4]),
    .Func3(spliter_1_funct[3]), .Func2(spliter_1_funct[2]), .Func1(spliter_1_funct[1]),
    .Func0(spliter_1_funct[0]), .a(display2_controller_1_a), .b(display2_controller_1_b),
    .c(display2_controller_1_c), .d(display2_controller_1_d), .e(display2_controller_1_e),
    .f(display2_controller_1_f), .g(display2_controller_1_g));
  display3_controller display3_controller_1 (
    .Op5(spliter_1_op[5]), .Op4(spliter_1_op[4]), .Op3(spliter_1_op[3]), .Op2(spliter_1_op[2]),
    .Op1(spliter_1_op[1]), .Op0(spliter_1_op[0]), .Func5(spliter_1_funct[5]), .Func4(spliter_1_funct[4]),
    .Func3(spliter_1_funct[3]), .Func2(spliter_1_funct[2]), .Func1(spliter_1_funct[1]),
    .Func0(spliter_1_funct[0]), .a(display3_controller_1_a), .b(display3_controller_1_b),
    .c(display3_controller_1_c), .d(display3_controller_1_d), .e(display3_controller_1_e),
    .f(display3_controller_1_f), .g(display3_controller_1_g));
  display4_controller display4_controller_1 (
    .Op5(spliter_1_op[5]), .Op4(spliter_1_op[4]), .Op3(spliter_1_op[3]), .Op2(spliter_1_op[2]),
    .Op1(spliter_1_op[1]), .Op0(spliter_1_op[0]), .Func5(spliter_1_funct[5]), .Func4(spliter_1_funct[4]),
    .Func3(spliter_1_funct[3]), .Func2(spliter_1_funct[2]), .Func1(spliter_1_funct[1]),
    .Func0(spliter_1_funct[0]), .a(display4_controller_1_a), .b(display4_controller_1_b),
    .c(display4_controller_1_c), .d(display4_controller_1_d), .e(display4_controller_1_e),
    .f(display4_controller_1_f), .g(display4_controller_1_g));
  _7_Segment_Display u_7_segment_display_1 (
    .g(display_controller_1_g), .f(display_controller_1_f), .a(display_controller_1_a),
    .b(display_controller_1_b), .e(display_controller_1_e), .d(display_controller_1_d),
    .c(display_controller_1_c));  // open: dp
  // Probe on Rw
  _7_Segment_Display u_7_segment_display_2 (
    .g(display2_controller_1_g), .f(display2_controller_1_f), .a(display2_controller_1_a),
    .b(display2_controller_1_b), .e(display2_controller_1_e), .d(display2_controller_1_d),
    .c(display2_controller_1_c));  // open: dp
  // Probe on Rs
  registers registers_1 (
    .busW(multiplexer_7_out), .Reset(Reset), .Clock(Clock), .busA(registers_1_busa), .busB(registers_1_busb),
    .Enable_RegWr(RegWrite), .Rw(Rw), .Ra(Rs), .Rb(Rt));
  _7_Segment_Display u_7_segment_display_3 (
    .g(display3_controller_1_g), .f(display3_controller_1_f), .a(display3_controller_1_a),
    .b(display3_controller_1_b), .e(display3_controller_1_e), .d(display3_controller_1_d),
    .c(display3_controller_1_c));  // open: dp
  // Probe on Rt
  _7_Segment_Display u_7_segment_display_4 (
    .g(display4_controller_1_g), .f(display4_controller_1_f), .a(display4_controller_1_a),
    .b(display4_controller_1_b), .e(display4_controller_1_e), .d(display4_controller_1_d),
    .c(display4_controller_1_c));  // open: dp
  assign SExtender = {{16{1'b0}}, Imm16};  // Bit_Extender bit_extender_2
  Multiplexer #(.width(32), .enable("false")) multiplexer_6 (
    .in0(registers_1_busb), .in1(SExtender), .out(multiplexer_6_out), .sel(ALUSrc));
  ALU alu_1 (
    .in_5(registers_1_busa), .in_6(multiplexer_6_out), .ALUCtrl3(ALUCtrl3), .ALUCtrl2(ALUCtrl2),
    .ALUCtrl1(ALUCtrl1), .ALUCtrl0(ALUCtrl0), .Resultado({alu_1_resultado_2, alu_1_resultado}), .out_8(Zero));
  assign controlled_buffer_1_out = MemWrite ? registers_1_busb : 32'bz;  // Controlled_Buffer controlled_buffer_1
  not not_2 (not_2_out, MemWrite);
  RAM #(.addrWidth(24), .dataWidth(32)) ram_2 (
    .addr(alu_1_resultado), .data(controlled_buffer_1_out), .clk(Clock), .ld(not_2_out), .clr(Reset));  // open: sel
  Multiplexer #(.width(32), .enable("false")) multiplexer_7 (
    .in0({alu_1_resultado_2, alu_1_resultado}), .in1(controlled_buffer_1_out), .out(multiplexer_7_out),
    .sel(MemtoReg));

  // Notes on the sheet:
  //   Registros
  //   SingExtender
  //   BusB
  //   ALU
  //   Address
  //   Data Memory
endmodule

module registers (
  input  Enable_RegWr,
  input  [4:0] Rw,
  input  [4:0] Ra,
  input  [4:0] Rb,
  input  [31:0] busW,
  input  Reset,
  input  Clock,
  output [31:0] busA,
  output [31:0] busB
);

  wire S0, S1, S2, S3, S4, S5, S6, S7, S8, S9, S10, S11, S12, S13, S14, S15, S16, S17, S18, S19, S20, S21,
       S22, S23, S24, S25, S26, S27, S28, S29, S30, S31;
  wire [31:0] R0, R1, R2, R3, R4, R5, R6, R7, R8, R9, R10, R11, R12, R13, R14, R15, R16, R17, R18, R19, R20,
       R21, R22, R23, R24, R25, R26, R27, R28, R29, R30, R31;

  Decoder #(.select(5), .disabled(0)) decoder_1 (
    .out0(S0), .out1(S1), .out2(S2), .out3(S3), .out4(S4), .out5(S5), .out6(S6), .out7(S7), .out8(S8),
    .out9(S9), .out10(S10), .out11(S11), .out12(S12), .out13(S13), .out14(S14), .out15(S15), .out16(S16),
    .out17(S17), .out18(S18), .out19(S19), .out20(S20), .out21(S21), .out22(S22), .out23(S23), .out24(S24),
    .out25(S25), .out26(S26), .out27(S27), .out28(S28), .out29(S29), .out30(S30), .out31(S31), .sel(Rw),
    .en(Enable_RegWr));
  Register #(.width(32)) zero (.D(busW), .en(S0), .Q(R0), .clk(Clock), .clr(Reset));
  Register #(.width(32)) t0 (.D(busW), .en(S8), .Q(R8), .clk(Clock), .clr(Reset));
  Register #(.width(32)) u_s0 (.D(busW), .en(S16), .Q(R16), .clk(Clock), .clr(Reset));
  Register #(.width(32)) t8 (.D(busW), .en(S24), .Q(R24), .clk(Clock), .clr(Reset));
  Register #(.width(32)) at (.D(busW), .en(S1), .Q(R1), .clk(Clock), .clr(Reset));
  Register #(.width(32)) t1 (.D(busW), .en(S9), .Q(R9), .clk(Clock), .clr(Reset));
  Register #(.width(32)) u_s1 (.D(busW), .en(S17), .Q(R17), .clk(Clock), .clr(Reset));
  Register #(.width(32)) t9 (.D(busW), .en(S25), .Q(R25), .clk(Clock), .clr(Reset));
  Multiplexer #(.select(5), .width(32), .enable("false")) multiplexer_1 (
    .in0(R0), .in1(R1), .in2(R2), .in3(R3), .in4(R4), .in5(R5), .in6(R6), .in7(R7), .in8(R8), .in9(R9),
    .in10(R10), .in11(R11), .in12(R12), .in13(R13), .in14(R14), .in15(R15), .in16(R16), .in17(R17),
    .in18(R18), .in19(R19), .in20(R20), .in21(R21), .in22(R22), .in23(R23), .in24(R24), .in25(R25),
    .in26(R26), .in27(R27), .in28(R28), .in29(R29), .in30(R30), .in31(R31), .out(busA), .sel(Ra));
  Register #(.width(32)) v0 (.D(busW), .en(S2), .Q(R2), .clk(Clock), .clr(Reset));
  Register #(.width(32)) t2 (.D(busW), .en(S10), .Q(R10), .clk(Clock), .clr(Reset));
  Register #(.width(32)) u_s2 (.D(busW), .en(S18), .Q(R18), .clk(Clock), .clr(Reset));
  Register #(.width(32)) k0 (.D(busW), .en(S26), .Q(R26), .clk(Clock), .clr(Reset));
  Register #(.width(32)) v1 (.D(busW), .en(S3), .Q(R3), .clk(Clock), .clr(Reset));
  Register #(.width(32)) t3 (.D(busW), .en(S11), .Q(R11), .clk(Clock), .clr(Reset));
  Register #(.width(32)) u_s3 (.D(busW), .en(S19), .Q(R19), .clk(Clock), .clr(Reset));
  Register #(.width(32)) k1 (.D(busW), .en(S27), .Q(R27), .clk(Clock), .clr(Reset));
  Register #(.width(32)) a0 (.D(busW), .en(S4), .Q(R4), .clk(Clock), .clr(Reset));
  Register #(.width(32)) t4 (.D(busW), .en(S12), .Q(R12), .clk(Clock), .clr(Reset));
  Register #(.width(32)) u_s4 (.D(busW), .en(S20), .Q(R20), .clk(Clock), .clr(Reset));
  Register #(.width(32)) gp (.D(busW), .en(S28), .Q(R28), .clk(Clock), .clr(Reset));
  Register #(.width(32)) a1 (.D(busW), .en(S5), .Q(R5), .clk(Clock), .clr(Reset));
  Register #(.width(32)) t5 (.D(busW), .en(S13), .Q(R13), .clk(Clock), .clr(Reset));
  Register #(.width(32)) u_s5 (.D(busW), .en(S21), .Q(R21), .clk(Clock), .clr(Reset));
  Register #(.width(32)) sp (.D(busW), .en(S29), .Q(R29), .clk(Clock), .clr(Reset));
  Multiplexer #(.select(5), .width(32), .enable("false")) multiplexer_2 (
    .in0(R0), .in1(R1), .in2(R2), .in3(R3), .in4(R4), .in5(R5), .in6(R6), .in7(R7), .in8(R8), .in9(R9),
    .in10(R10), .in11(R11), .in12(R12), .in13(R13), .in14(R14), .in15(R15), .in16(R16), .in17(R17),
    .in18(R18), .in19(R19), .in20(R20), .in21(R21), .in22(R22), .in23(R23), .in24(R24), .in25(R25),
    .in26(R26), .in27(R27), .in28(R28), .in29(R29), .in30(R30), .in31(R31), .out(busB), .sel(Rb));
  Register #(.width(32)) a2 (.D(busW), .en(S6), .Q(R6), .clk(Clock), .clr(Reset));
  Register #(.width(32)) t6 (.D(busW), .en(S14), .Q(R14), .clk(Clock), .clr(Reset));
  Register #(.width(32)) u_s6 (.D(busW), .en(S22), .Q(R22), .clk(Clock), .clr(Reset));
  Register #(.width(32)) fp (.D(busW), .en(S30), .Q(R30), .clk(Clock), .clr(Reset));
  Register #(.width(32)) a3 (.D(busW), .en(S7), .Q(R7), .clk(Clock), .clr(Reset));
  Register #(.width(32)) t7 (.D(busW), .en(S15), .Q(R15), .clk(Clock), .clr(Reset));
  Register #(.width(32)) u_s7 (.D(busW), .en(S23), .Q(R23), .clk(Clock), .clr(Reset));
  Register #(.width(32)) u_ra (.D(busW), .en(S31), .Q(R31), .clk(Clock), .clr(Reset));

  // Other names for the same wires on the sheet: C = Clock; MuxA[31:0] = busA; MuxB[31:0] = busB; R = Reset;
  //   RegWr = Enable_RegWr
endmodule

module spliter (
  input  [31:0] in_1,
  output [5:0] funct,
  output [4:0] shamt,
  output [4:0] rd,
  output [4:0] rt,
  output [4:0] rs,
  output [5:0] op,
  output [25:0] address,
  output [15:0] offset
);


  assign address = in_1[25:0];
  assign funct = in_1[5:0];
  assign offset = in_1[15:0];
  assign op = in_1[31:26];
  assign rd = in_1[15:11];
  assign rs = in_1[25:21];
  assign rt = in_1[20:16];
  assign shamt = in_1[10:6];
endmodule

// Control Unit
module control (
  input  [5:0] OPCODE,
  output Jump,
  output RegDst,
  output ALUSrc,
  output MemtoReg,
  output RegWrite,
  output MemRead,
  output MemWrite,
  output Branch,
  output ALUOp1,
  output bne,
  output ALUOp0
);

  wire control_opcode_instruction_1_addi, control_opcode_instruction_1_beq,
       control_opcode_instruction_1_jump, control_opcode_instruction_1_lw,
       control_opcode_instruction_1_rformat, control_opcode_instruction_1_sw;

  control_instruction__output control_instruction_output_1 (
    .Rformat(control_opcode_instruction_1_rformat), .lw(control_opcode_instruction_1_lw),
    .sw(control_opcode_instruction_1_sw), .beq(control_opcode_instruction_1_beq),
    .addi(control_opcode_instruction_1_addi), .jump(control_opcode_instruction_1_jump), .RegDat(RegDst),
    .ALUSrc(ALUSrc), .MemtoReg(MemtoReg), .RegWrite(RegWrite), .MemRead(MemRead), .MemWrite(MemWrite),
    .Branch(Branch), .ALUOp1(ALUOp1), .ALUOp0(ALUOp0), .J(Jump));
  control_opcode__instruction control_opcode_instruction_1 (
    .Op5(OPCODE[5]), .Op4(OPCODE[4]), .Op3(OPCODE[3]), .Op2(OPCODE[2]), .Op1(OPCODE[1]), .Op0(OPCODE[0]),
    .Rformat(control_opcode_instruction_1_rformat), .lw(control_opcode_instruction_1_lw),
    .sw(control_opcode_instruction_1_sw), .beq(control_opcode_instruction_1_beq),
    .addi(control_opcode_instruction_1_addi), .jump(control_opcode_instruction_1_jump), .bne(bne));
endmodule

module lw (
  input  Op5,
  input  Op4,
  input  Op3,
  input  Op2,
  input  Op1,
  input  Op0,
  output lw
);

  wire not_1_out, not_2_out, not_3_out;

  not not_1 (not_1_out, Op4);
  not not_2 (not_2_out, Op3);
  not not_3 (not_3_out, Op2);
  and and_1 (lw, Op5, not_1_out, not_2_out, not_3_out, Op1, Op0);
endmodule

module sw (
  input  Op5,
  input  Op4,
  input  Op3,
  input  Op2,
  input  Op1,
  input  Op0,
  output sw
);

  wire not_1_out, not_2_out;

  not not_1 (not_1_out, Op4);
  not not_2 (not_2_out, Op2);
  and and_1 (sw, Op5, not_1_out, Op3, not_2_out, Op1, Op0);
endmodule

module beq (
  input  Op5,
  input  Op4,
  input  Op3,
  input  Op2,
  input  Op1,
  input  Op0,
  output sw,
  output beq
);

  wire not_1_out, not_2_out, not_3_out, not_4_out, not_5_out, not_6_out, not_7_out;

  not not_1 (not_1_out, Op4);
  not not_2 (not_2_out, Op2);
  not not_3 (not_3_out, Op5);
  not not_4 (not_4_out, Op4);
  not not_5 (not_5_out, Op3);
  not not_6 (not_6_out, Op1);
  not not_7 (not_7_out, Op0);
  and and_1 (sw, Op5, not_1_out, Op3, not_2_out, Op1, Op0);
  and and_2 (beq, not_3_out, not_4_out, not_5_out, Op2, not_6_out, not_7_out);
endmodule

module control_opcode__instruction (
  input  Op5,
  input  Op4,
  input  Op3,
  input  Op2,
  input  Op1,
  input  Op0,
  output Rformat,
  output lw,
  output sw,
  output beq,
  output addi,
  output jump,
  output bne
);

  wire not_1_out, not_2_out, not_3_out, not_4_out, not_5_out, not_6_out, not_7_out, not_8_out, not_9_out,
       not_10_out, not_11_out, not_12_out, not_13_out, not_14_out, not_15_out, not_16_out, not_17_out,
       not_18_out, not_19_out, not_20_out, not_21_out, not_22_out, not_23_out, not_24_out, not_25_out,
       not_26_out, not_27_out, not_28_out, not_29_out;

  not not_1 (not_1_out, Op5);
  not not_2 (not_2_out, Op4);
  not not_3 (not_3_out, Op3);
  not not_4 (not_4_out, Op2);
  not not_5 (not_5_out, Op1);
  not not_6 (not_6_out, Op0);
  not not_7 (not_7_out, Op4);
  not not_8 (not_8_out, Op3);
  not not_9 (not_9_out, Op2);
  not not_10 (not_10_out, Op4);
  not not_11 (not_11_out, Op2);
  not not_12 (not_12_out, Op5);
  not not_13 (not_13_out, Op4);
  not not_14 (not_14_out, Op3);
  not not_15 (not_15_out, Op1);
  not not_16 (not_16_out, Op5);
  not not_17 (not_17_out, Op4);
  not not_18 (not_18_out, Op2);
  not not_19 (not_19_out, Op1);
  not not_20 (not_20_out, Op0);
  not not_21 (not_21_out, Op5);
  not not_22 (not_22_out, Op4);
  not not_23 (not_23_out, Op3);
  not not_24 (not_24_out, Op2);
  not not_25 (not_25_out, Op0);
  not not_26 (not_26_out, Op5);
  not not_27 (not_27_out, Op4);
  not not_28 (not_28_out, Op3);
  not not_29 (not_29_out, Op1);
  and and_1 (Rformat, not_1_out, not_2_out, not_3_out, not_4_out, not_5_out, not_6_out);
  and and_2 (lw, Op5, not_7_out, not_8_out, not_9_out, Op1, Op0);
  and and_3 (sw, Op5, not_10_out, Op3, not_11_out, Op1, Op0);
  and and_4 (beq, not_12_out, not_13_out, not_14_out, Op2, not_15_out);
  and and_5 (addi, not_16_out, not_17_out, Op3, not_18_out, not_19_out, not_20_out);
  and and_6 (jump, not_21_out, not_22_out, not_23_out, not_24_out, Op1, not_25_out);
  and and_7 (bne, not_26_out, not_27_out, not_28_out, Op2, not_29_out, Op0);
endmodule

module control_instruction__output (
  input  Rformat,
  input  lw,
  input  sw,
  input  beq,
  input  addi,
  input  jump,
  output RegDat,
  output ALUSrc,
  output MemtoReg,
  output RegWrite,
  output MemRead,
  output MemWrite,
  output Branch,
  output ALUOp1,
  output ALUOp0,
  output J
);

  wire and_2_out, and_3_out, and_4_out, and_6_out, and_7_out, and_8_out, not_1_out, not_2_out, not_3_out,
       not_4_out, not_5_out, not_6_out, not_7_out, not_8_out, not_9_out, not_10_out, not_11_out, not_12_out,
       not_13_out, not_14_out, not_15_out, not_16_out, not_17_out, not_18_out, not_19_out, not_20_out,
       not_21_out, not_22_out, not_23_out, not_24_out, not_25_out, not_26_out, not_27_out, not_28_out,
       not_29_out, not_30_out, not_31_out, not_32_out, not_33_out, not_34_out, not_35_out, not_36_out,
       not_37_out, not_38_out, not_39_out, not_40_out, not_41_out, not_42_out, not_43_out, not_44_out,
       not_45_out, not_46_out;

  not not_1 (not_1_out, lw);
  not not_2 (not_2_out, sw);
  not not_3 (not_3_out, beq);
  not not_4 (not_4_out, Rformat);
  not not_5 (not_5_out, sw);
  not not_6 (not_6_out, beq);
  not not_7 (not_7_out, jump);
  not not_8 (not_8_out, Rformat);
  not not_9 (not_9_out, lw);
  not not_10 (not_10_out, beq);
  not not_11 (not_11_out, Rformat);
  not not_12 (not_12_out, sw);
  not not_13 (not_13_out, beq);
  not not_14 (not_14_out, Rformat);
  not not_15 (not_15_out, sw);
  not not_16 (not_16_out, beq);
  not not_17 (not_17_out, Rformat);
  not not_18 (not_18_out, sw);
  not not_19 (not_19_out, beq);
  not not_20 (not_20_out, jump);
  not not_21 (not_21_out, Rformat);
  not not_22 (not_22_out, sw);
  not not_23 (not_23_out, beq);
  not not_24 (not_24_out, lw);
  not not_25 (not_25_out, sw);
  not not_26 (not_26_out, beq);
  not not_27 (not_27_out, Rformat);
  not not_28 (not_28_out, sw);
  not not_29 (not_29_out, beq);
  not not_30 (not_30_out, Rformat);
  not not_31 (not_31_out, lw);
  not not_32 (not_32_out, beq);
  not not_33 (not_33_out, Rformat);
  not not_34 (not_34_out, lw);
  not not_35 (not_35_out, sw);
  not not_36 (not_36_out, lw);
  not not_37 (not_37_out, sw);
  not not_38 (not_38_out, beq);
  not not_39 (not_39_out, Rformat);
  not not_40 (not_40_out, lw);
  not not_41 (not_41_out, sw);
  not not_42 (not_42_out, Rformat);
  not not_43 (not_43_out, lw);
  not not_44 (not_44_out, sw);
  not not_45 (not_45_out, beq);
  not not_46 (not_46_out, addi);
  and and_1 (RegDat, Rformat, not_1_out, not_2_out, not_3_out);
  and and_2 (and_2_out, not_4_out, not_5_out, not_6_out, addi, not_7_out);
  and and_3 (and_3_out, not_8_out, not_9_out, sw, not_10_out);
  and and_4 (and_4_out, not_11_out, lw, not_12_out, not_13_out);
  and and_5 (MemtoReg, not_14_out, lw, not_15_out, not_16_out);
  and and_6 (and_6_out, not_17_out, not_18_out, not_19_out, addi, not_20_out);
  and and_7 (and_7_out, not_21_out, lw, not_22_out, not_23_out);
  and and_8 (and_8_out, Rformat, not_24_out, not_25_out, not_26_out);
  and and_9 (MemRead, not_27_out, lw, not_28_out, not_29_out);
  and and_10 (MemWrite, not_30_out, not_31_out, sw, not_32_out);
  and and_11 (Branch, not_33_out, not_34_out, not_35_out, beq);
  and and_12 (ALUOp1, Rformat, not_36_out, not_37_out, not_38_out);
  and and_13 (ALUOp0, not_39_out, not_40_out, not_41_out, beq);
  and and_14 (J, not_42_out, not_43_out, not_44_out, not_45_out, not_46_out, jump);
  or or_1 (ALUSrc, and_2_out, and_3_out, and_4_out);
  or or_2 (RegWrite, and_6_out, and_7_out, and_8_out);
endmodule

// ALU Control
module ALUControl (
  input  ALUOp1,
  input  ALUOp0,
  input  F5,
  input  F4,
  input  F3,
  input  F2,
  input  F1,
  input  F0,
  output ALUCtrl3,
  output ALUCtrl2,
  output ALUCtrl1,
  output ALUCtrl0
);

  wire and_1_out, and_2_out, and_3_out, and_4_out, and_5_out, and_6_out, and_7_out, and_8_out, and_9_out,
       and_10_out, and_11_out, not_1_out, not_2_out, not_3_out, not_4_out, not_5_out;

  not not_1 (not_1_out, F2);
  and and_1 (and_1_out, ALUOp1, not_1_out, F0);
  and and_2 (and_2_out, ALUOp1, F2, F1);
  and and_3 (and_3_out, ALUOp1, F3, not_2_out);
  not not_2 (not_2_out, F1);
  and and_4 (and_4_out, ALUOp1, ALUOp0);
  not not_3 (not_3_out, F2);
  and and_5 (and_5_out, ALUOp1, not_3_out, F0);
  and and_6 (and_6_out, ALUOp1, F1);
  and and_7 (and_7_out, ALUOp1, F3);
  not not_4 (not_4_out, ALUOp1);
  not not_5 (not_5_out, F2);
  and and_8 (and_8_out, ALUOp1, F0);
  and and_9 (and_9_out, ALUOp1, F2, F1);
  and and_10 (and_10_out, ALUOp1, F3);
  and and_11 (and_11_out, ALUOp1, ALUOp0);
  or or_1 (ALUCtrl3, and_1_out, and_2_out, and_3_out, and_4_out);
  or or_2 (ALUCtrl2, ALUOp0, and_5_out, and_6_out, and_7_out);
  or or_3 (ALUCtrl1, not_4_out, not_5_out, F1, F3, ALUOp0);
  or or_4 (ALUCtrl0, and_8_out, and_9_out, and_10_out, and_11_out);
endmodule

module display_controller (
  input  Op5,
  input  Op4,
  input  Op3,
  input  Op2,
  input  Op1,
  input  Op0,
  input  Func5,
  input  Func4,
  input  Func3,
  input  Func2,
  input  Func1,
  input  Func0,
  output a,
  output b,
  output c,
  output d,
  output e,
  output f,
  output g
);

  wire display_norinstruction_1_a, display_norinstruction_1_b, display_norinstruction_1_c,
       display_norinstruction_1_d, display_norinstruction_1_e, display_norinstruction_1_f,
       display_norinstruction_1_g, display_rinstruction_1_a, display_rinstruction_1_b,
       display_rinstruction_1_c, display_rinstruction_1_d, display_rinstruction_1_e,
       display_rinstruction_1_f, display_rinstruction_1_g, not_1_out, or_1_out;

  or or_1 (or_1_out, Op0, Op1, Op2, Op3, Op4, Op5);
  display_noRinstruction display_norinstruction_1 (
    .Op5(Op5), .Op4(Op4), .Op3(Op3), .Op2(Op2), .Op1(Op1), .Op0(Op0), .Enable(or_1_out),
    .a(display_norinstruction_1_a), .b(display_norinstruction_1_b), .c(display_norinstruction_1_c),
    .d(display_norinstruction_1_d), .e(display_norinstruction_1_e), .f(display_norinstruction_1_f),
    .g(display_norinstruction_1_g));
  not not_1 (not_1_out, or_1_out);
  display_Rinstruction display_rinstruction_1 (
    .Func5(Func5), .Func4(Func4), .Func3(Func3), .Func2(Func2), .Func1(Func1), .Func0(Func0),
    .Enable(not_1_out), .a(display_rinstruction_1_a), .b(display_rinstruction_1_b),
    .c(display_rinstruction_1_c), .d(display_rinstruction_1_d), .e(display_rinstruction_1_e),
    .f(display_rinstruction_1_f), .g(display_rinstruction_1_g));
  or or_2 (a, display_norinstruction_1_a, display_rinstruction_1_a);
  or or_3 (b, display_norinstruction_1_b, display_rinstruction_1_b);
  or or_4 (c, display_norinstruction_1_c, display_rinstruction_1_c);
  or or_5 (d, display_norinstruction_1_d, display_rinstruction_1_d);
  or or_6 (e, display_norinstruction_1_e, display_rinstruction_1_e);
  or or_7 (f, display_norinstruction_1_f, display_rinstruction_1_f);
  or or_8 (g, display_norinstruction_1_g, display_rinstruction_1_g);
endmodule

// Function Instructions
module funcInstructions (
  input  Op5,
  input  Op4,
  input  Op3,
  input  Op2,
  input  Op1,
  input  Op0,
  input  in_7,
  output Load,
  output Store,
  output Addi,
  output Branch,
  output Jump
);

  wire and_1_out, and_2_out, and_3_out, and_4_out, and_5_out, not_1_out, not_2_out, not_3_out, not_4_out,
       not_5_out, not_6_out, not_7_out, not_8_out, not_9_out, not_10_out, not_11_out, not_12_out, not_13_out,
       not_14_out, not_15_out, not_16_out, not_17_out, not_18_out, not_19_out, not_20_out;

  not not_1 (not_1_out, Op4);
  not not_2 (not_2_out, Op3);
  not not_3 (not_3_out, Op2);
  not not_4 (not_4_out, Op4);
  not not_5 (not_5_out, Op2);
  not not_6 (not_6_out, Op5);
  not not_7 (not_7_out, Op4);
  not not_8 (not_8_out, Op2);
  not not_9 (not_9_out, Op1);
  not not_10 (not_10_out, Op0);
  not not_11 (not_11_out, Op5);
  not not_12 (not_12_out, Op4);
  not not_13 (not_13_out, Op3);
  not not_14 (not_14_out, Op1);
  not not_15 (not_15_out, Op0);
  not not_16 (not_16_out, Op5);
  not not_17 (not_17_out, Op4);
  not not_18 (not_18_out, Op3);
  not not_19 (not_19_out, Op2);
  not not_20 (not_20_out, Op0);
  and and_1 (and_1_out, Op5, not_1_out, not_2_out, not_3_out, Op1, Op0);
  and and_2 (and_2_out, Op5, not_4_out, Op3, not_5_out, Op1, Op0);
  and and_3 (and_3_out, not_6_out, not_7_out, Op3, not_8_out, not_9_out, not_10_out);
  and and_4 (and_4_out, not_11_out, not_12_out, not_13_out, Op2, not_14_out, not_15_out);
  and and_5 (and_5_out, not_16_out, not_17_out, not_18_out, not_19_out, Op1, not_20_out);
  and and_6 (Load, and_1_out, in_7);
  and and_7 (Store, and_2_out, in_7);
  and and_8 (Addi, and_3_out, in_7);
  and and_9 (Branch, and_4_out, in_7);
  and and_10 (Jump, and_5_out, in_7);
endmodule

// Opcode Instructions
module Op_Instructions (
  input  F5,
  input  F4,
  input  F3,
  input  F2,
  input  F1,
  input  F0,
  input  Enable,
  output add,
  output sub,
  output AND,
  output OR
);

  wire and_1_out, and_2_out, and_3_out, and_4_out, not_1_out, not_2_out, not_3_out, not_4_out, not_5_out,
       not_6_out, not_7_out, not_8_out, not_9_out, not_10_out, not_11_out, not_12_out, not_13_out,
       not_14_out, not_15_out, not_16_out;

  not not_1 (not_1_out, F4);
  not not_2 (not_2_out, F3);
  not not_3 (not_3_out, F2);
  not not_4 (not_4_out, F1);
  not not_5 (not_5_out, F0);
  not not_6 (not_6_out, F4);
  not not_7 (not_7_out, F3);
  not not_8 (not_8_out, F2);
  not not_9 (not_9_out, F0);
  not not_10 (not_10_out, F4);
  not not_11 (not_11_out, F3);
  not not_12 (not_12_out, F1);
  not not_13 (not_13_out, F0);
  not not_14 (not_14_out, F4);
  not not_15 (not_15_out, F3);
  not not_16 (not_16_out, F1);
  and and_1 (and_1_out, F5, not_1_out, not_2_out, not_3_out, not_4_out, not_5_out);
  and and_2 (and_2_out, F5, not_6_out, not_7_out, not_8_out, F1, not_9_out);
  and and_3 (and_3_out, F5, not_10_out, not_11_out, F2, not_12_out, not_13_out);
  and and_4 (and_4_out, F5, not_14_out, not_15_out, F2, not_16_out, F0);
  and and_5 (add, and_1_out, Enable);
  and and_6 (sub, and_2_out, Enable);
  and and_7 (AND, and_3_out, Enable);
  and and_8 (OR, and_4_out, Enable);
endmodule

module display_noRinstruction (
  input  Op5,
  input  Op4,
  input  Op3,
  input  Op2,
  input  Op1,
  input  Op0,
  input  Enable,
  output a,
  output b,
  output c,
  output d,
  output e,
  output f,
  output g
);

  wire display_norinstruction_inside_1_a, display_norinstruction_inside_1_b,
       display_norinstruction_inside_1_c, display_norinstruction_inside_1_d,
       display_norinstruction_inside_1_e, display_norinstruction_inside_1_f,
       display_norinstruction_inside_1_g;

  display_noRinstruction_inside display_norinstruction_inside_1 (
    .Op5(Op5), .Op4(Op4), .Op3(Op3), .Op2(Op2), .Op1(Op1), .Op0(Op0), .a(display_norinstruction_inside_1_a),
    .b(display_norinstruction_inside_1_b), .c(display_norinstruction_inside_1_c),
    .d(display_norinstruction_inside_1_d), .e(display_norinstruction_inside_1_e),
    .f(display_norinstruction_inside_1_f), .g(display_norinstruction_inside_1_g));
  and and_1 (a, display_norinstruction_inside_1_a, Enable);
  and and_2 (b, display_norinstruction_inside_1_b, Enable);
  and and_3 (c, display_norinstruction_inside_1_c, Enable);
  and and_4 (d, display_norinstruction_inside_1_d, Enable);
  and and_5 (e, display_norinstruction_inside_1_e, Enable);
  and and_6 (f, display_norinstruction_inside_1_f, Enable);
  and and_7 (g, display_norinstruction_inside_1_g, Enable);
endmodule

module display_Rinstruction (
  input  Func5,
  input  Func4,
  input  Func3,
  input  Func2,
  input  Func1,
  input  Func0,
  input  Enable,
  output a,
  output b,
  output c,
  output d,
  output e,
  output f,
  output g
);

  wire display_rinstruction_inside_1_a, display_rinstruction_inside_1_b, display_rinstruction_inside_1_c,
       display_rinstruction_inside_1_d, display_rinstruction_inside_1_e, display_rinstruction_inside_1_f,
       display_rinstruction_inside_1_g;

  display_Rinstruction_inside display_rinstruction_inside_1 (
    .Func5(Func5), .Func4(Func4), .Func3(Func3), .Func2(Func2), .Func1(Func1), .Func0(Func0),
    .a(display_rinstruction_inside_1_a), .b(display_rinstruction_inside_1_b),
    .c(display_rinstruction_inside_1_c), .d(display_rinstruction_inside_1_d),
    .e(display_rinstruction_inside_1_e), .f(display_rinstruction_inside_1_f),
    .g(display_rinstruction_inside_1_g));
  and and_1 (a, display_rinstruction_inside_1_a, Enable);
  and and_2 (b, display_rinstruction_inside_1_b, Enable);
  and and_3 (c, display_rinstruction_inside_1_c, Enable);
  and and_4 (d, display_rinstruction_inside_1_d, Enable);
  and and_5 (e, display_rinstruction_inside_1_e, Enable);
  and and_6 (f, display_rinstruction_inside_1_f, Enable);
  and and_7 (g, display_rinstruction_inside_1_g, Enable);
endmodule

module display_noRinstruction_inside (
  input  Op5,
  input  Op4,
  input  Op3,
  input  Op2,
  input  Op1,
  input  Op0,
  output a,
  output b,
  output c,
  output d,
  output e,
  output f,
  output g
);

  wire and_1_out, and_2_out, and_3_out, and_4_out, and_5_out, and_6_out, and_7_out, and_8_out, and_9_out,
       and_10_out, and_11_out, and_12_out, and_13_out, and_14_out, and_15_out, and_16_out, and_17_out,
       and_18_out, and_19_out, and_20_out, and_21_out, not_1_out, not_2_out, not_3_out, not_4_out, not_5_out,
       not_6_out, not_7_out, not_8_out, not_9_out, not_10_out, not_11_out, not_12_out, not_13_out,
       not_14_out, not_15_out, not_16_out, not_17_out, not_18_out, not_19_out, not_20_out, not_21_out,
       not_22_out, not_23_out, not_24_out, not_25_out, not_26_out, not_27_out, not_28_out, not_29_out,
       not_30_out, not_31_out, not_32_out, not_33_out, not_34_out, not_35_out, not_36_out, not_37_out,
       not_38_out, not_39_out, not_40_out, not_41_out, not_42_out, not_43_out, not_44_out, not_45_out,
       not_46_out, not_47_out, not_48_out, not_49_out, not_50_out, not_51_out, not_52_out, not_53_out,
       not_54_out, not_55_out, not_56_out, not_57_out, not_58_out, not_59_out, not_60_out, not_61_out,
       not_62_out, not_63_out, not_64_out, not_65_out, not_66_out, not_67_out, not_68_out, not_69_out,
       not_70_out, not_71_out, not_72_out, not_73_out, not_74_out, not_75_out, not_76_out, not_77_out,
       not_78_out, not_79_out, not_80_out, not_81_out, not_82_out, not_83_out, not_84_out, not_85_out,
       not_86_out, not_87_out, not_88_out;

  not not_1 (not_1_out, Op5);
  not not_2 (not_2_out, Op4);
  not not_3 (not_3_out, Op3);
  not not_4 (not_4_out, Op2);
  not not_5 (not_5_out, Op0);
  not not_6 (not_6_out, Op5);
  not not_7 (not_7_out, Op4);
  not not_8 (not_8_out, Op2);
  not not_9 (not_9_out, Op1);
  not not_10 (not_10_out, Op0);
  not not_11 (not_11_out, Op4);
  not not_12 (not_12_out, Op2);
  not not_13 (not_13_out, Op5);
  not not_14 (not_14_out, Op4);
  not not_15 (not_15_out, Op3);
  not not_16 (not_16_out, Op2);
  not not_17 (not_17_out, Op0);
  not not_18 (not_18_out, Op5);
  not not_19 (not_19_out, Op4);
  not not_20 (not_20_out, Op2);
  not not_21 (not_21_out, Op1);
  not not_22 (not_22_out, Op0);
  not not_23 (not_23_out, Op5);
  not not_24 (not_24_out, Op4);
  not not_25 (not_25_out, Op3);
  not not_26 (not_26_out, Op2);
  not not_27 (not_27_out, Op0);
  not not_28 (not_28_out, Op5);
  not not_29 (not_29_out, Op4);
  not not_30 (not_30_out, Op3);
  not not_31 (not_31_out, Op1);
  not not_32 (not_32_out, Op0);
  not not_33 (not_33_out, Op5);
  not not_34 (not_34_out, Op4);
  not not_35 (not_35_out, Op2);
  not not_36 (not_36_out, Op1);
  not not_37 (not_37_out, Op0);
  not not_38 (not_38_out, Op4);
  not not_39 (not_39_out, Op2);
  not not_40 (not_40_out, Op5);
  not not_41 (not_41_out, Op4);
  not not_42 (not_42_out, Op3);
  not not_43 (not_43_out, Op2);
  not not_44 (not_44_out, Op0);
  not not_45 (not_45_out, Op5);
  not not_46 (not_46_out, Op4);
  not not_47 (not_47_out, Op3);
  not not_48 (not_48_out, Op1);
  not not_49 (not_49_out, Op0);
  not not_50 (not_50_out, Op4);
  not not_51 (not_51_out, Op2);
  not not_52 (not_52_out, Op5);
  not not_53 (not_53_out, Op4);
  not not_54 (not_54_out, Op3);
  not not_55 (not_55_out, Op1);
  not not_56 (not_56_out, Op0);
  not not_57 (not_57_out, Op5);
  not not_58 (not_58_out, Op4);
  not not_59 (not_59_out, Op2);
  not not_60 (not_60_out, Op1);
  not not_61 (not_61_out, Op0);
  not not_62 (not_62_out, Op4);
  not not_63 (not_63_out, Op3);
  not not_64 (not_64_out, Op2);
  not not_65 (not_65_out, Op5);
  not not_66 (not_66_out, Op4);
  not not_67 (not_67_out, Op3);
  not not_68 (not_68_out, Op1);
  not not_69 (not_69_out, Op0);
  not not_70 (not_70_out, Op5);
  not not_71 (not_71_out, Op4);
  not not_72 (not_72_out, Op2);
  not not_73 (not_73_out, Op1);
  not not_74 (not_74_out, Op0);
  not not_75 (not_75_out, Op4);
  not not_76 (not_76_out, Op2);
  not not_77 (not_77_out, Op5);
  not not_78 (not_78_out, Op4);
  not not_79 (not_79_out, Op3);
  not not_80 (not_80_out, Op1);
  not not_81 (not_81_out, Op0);
  not not_82 (not_82_out, Op5);
  not not_83 (not_83_out, Op4);
  not not_84 (not_84_out, Op2);
  not not_85 (not_85_out, Op1);
  not not_86 (not_86_out, Op0);
  not not_87 (not_87_out, Op4);
  not not_88 (not_88_out, Op2);
  and and_1 (and_1_out, not_1_out, not_2_out, not_3_out, not_4_out, Op1, not_5_out);
  and and_2 (and_2_out, not_6_out, not_7_out, Op3, not_8_out, not_9_out, not_10_out);
  and and_3 (and_3_out, Op5, not_11_out, Op3, not_12_out, Op1, Op0);
  and and_4 (and_4_out, not_13_out, not_14_out, not_15_out, not_16_out, Op1, not_17_out);
  and and_5 (and_5_out, not_18_out, not_19_out, Op3, not_20_out, not_21_out, not_22_out);
  and and_6 (and_6_out, not_23_out, not_24_out, not_25_out, not_26_out, Op1, not_27_out);
  and and_7 (and_7_out, not_28_out, not_29_out, not_30_out, Op2, not_31_out, not_32_out);
  and and_8 (and_8_out, not_33_out, not_34_out, Op3, not_35_out, not_36_out, not_37_out);
  and and_9 (and_9_out, Op5, not_38_out, Op3, not_39_out, Op1, Op0);
  and and_10 (and_10_out, not_40_out, not_41_out, not_42_out, not_43_out, Op1, not_44_out);
  and and_11 (and_11_out, not_45_out, not_46_out, not_47_out, Op2, not_48_out, not_49_out);
  and and_12 (and_12_out, Op5, not_50_out, not_51_out, Op1, Op0);
  and and_13 (and_13_out, not_52_out, not_53_out, not_54_out, Op2, not_55_out, not_56_out);
  and and_14 (and_14_out, not_57_out, not_58_out, Op3, not_59_out, not_60_out, not_61_out);
  and and_15 (and_15_out, Op5, not_62_out, not_63_out, not_64_out, Op1, Op0);
  and and_16 (and_16_out, not_65_out, not_66_out, not_67_out, Op2, not_68_out, not_69_out);
  and and_17 (and_17_out, not_70_out, not_71_out, Op3, not_72_out, not_73_out, not_74_out);
  and and_18 (and_18_out, Op5, not_75_out, not_76_out, Op1, Op0);
  and and_19 (and_19_out, not_77_out, not_78_out, not_79_out, Op2, not_80_out, not_81_out);
  and and_20 (and_20_out, not_82_out, not_83_out, Op3, not_84_out, not_85_out, not_86_out);
  and and_21 (and_21_out, Op5, not_87_out, Op3, not_88_out, Op1, Op0);
  or or_1 (a, and_1_out, and_2_out, and_3_out);
  or or_2 (b, and_4_out, and_5_out);
  or or_3 (c, and_6_out, and_7_out, and_8_out, and_9_out);
  or or_4 (d, and_10_out, and_11_out, and_12_out);
  or or_5 (e, and_13_out, and_14_out, and_15_out);
  or or_6 (f, and_16_out, and_17_out, and_18_out);
  or or_7 (g, and_19_out, and_20_out, and_21_out);
endmodule

module display_Rinstruction_inside (
  input  Func5,
  input  Func4,
  input  Func3,
  input  Func2,
  input  Func1,
  input  Func0,
  output a,
  output b,
  output c,
  output d,
  output e,
  output f,
  output g
);

  wire and_1_out, and_2_out, and_3_out, and_4_out, and_5_out, and_6_out, and_7_out, and_8_out, and_9_out,
       and_10_out, and_11_out, and_12_out, not_1_out, not_2_out, not_3_out, not_4_out, not_5_out, not_6_out,
       not_7_out, not_8_out, not_9_out, not_10_out, not_11_out, not_12_out, not_13_out, not_14_out,
       not_15_out, not_16_out, not_17_out, not_18_out, not_19_out, not_20_out, not_21_out, not_22_out,
       not_23_out, not_24_out, not_25_out, not_26_out, not_27_out, not_28_out, not_29_out, not_30_out,
       not_31_out, not_32_out, not_33_out, not_34_out, not_35_out, not_36_out, not_37_out, not_38_out,
       not_39_out, not_40_out, not_41_out, not_42_out, not_43_out, not_44_out, not_45_out, not_46_out;

  not not_1 (not_1_out, Func4);
  not not_2 (not_2_out, Func3);
  not not_3 (not_3_out, Func2);
  not not_4 (not_4_out, Func0);
  not not_5 (not_5_out, Func4);
  not not_6 (not_6_out, Func3);
  not not_7 (not_7_out, Func1);
  not not_8 (not_8_out, Func4);
  not not_9 (not_9_out, Func3);
  not not_10 (not_10_out, Func1);
  not not_11 (not_11_out, Func0);
  not not_12 (not_12_out, Func4);
  not not_13 (not_13_out, Func3);
  not not_14 (not_14_out, Func1);
  not not_15 (not_15_out, Func4);
  not not_16 (not_16_out, Func3);
  not not_17 (not_17_out, Func2);
  not not_18 (not_18_out, Func0);
  not not_19 (not_19_out, Func4);
  not not_20 (not_20_out, Func3);
  not not_21 (not_21_out, Func1);
  not not_22 (not_22_out, Func4);
  not not_23 (not_23_out, Func3);
  not not_24 (not_24_out, Func2);
  not not_25 (not_25_out, Func0);
  not not_26 (not_26_out, Func4);
  not not_27 (not_27_out, Func3);
  not not_28 (not_28_out, Func1);
  not not_29 (not_29_out, Func4);
  not not_30 (not_30_out, Func3);
  not not_31 (not_31_out, Func1);
  not not_32 (not_32_out, Func0);
  not not_33 (not_33_out, Func4);
  not not_34 (not_34_out, Func3);
  not not_35 (not_35_out, Func1);
  not not_36 (not_36_out, Func4);
  not not_37 (not_37_out, Func3);
  not not_38 (not_38_out, Func2);
  not not_39 (not_39_out, Func0);
  not not_40 (not_40_out, Func4);
  not not_41 (not_41_out, Func3);
  not not_42 (not_42_out, Func1);
  not not_43 (not_43_out, Func4);
  not not_44 (not_44_out, Func3);
  not not_45 (not_45_out, Func2);
  not not_46 (not_46_out, Func0);
  and and_1 (and_1_out, Func5, not_1_out, not_2_out, not_3_out, not_4_out);
  and and_2 (and_2_out, Func5, not_5_out, not_6_out, Func2, not_7_out);
  and and_3 (and_3_out, Func5, not_8_out, not_9_out, not_10_out, not_11_out);
  and and_4 (and_4_out, Func5, not_12_out, not_13_out, Func2, not_14_out);
  and and_5 (and_5_out, Func5, not_15_out, not_16_out, not_17_out, not_18_out);
  and and_6 (and_6_out, Func5, not_19_out, not_20_out, Func2, not_21_out);
  and and_7 (and_7_out, Func5, not_22_out, not_23_out, not_24_out, Func1, not_25_out);
  and and_8 (and_8_out, Func5, not_26_out, not_27_out, Func2, not_28_out, Func0);
  and and_9 (and_9_out, Func5, not_29_out, not_30_out, not_31_out, not_32_out);
  and and_10 (and_10_out, Func5, not_33_out, not_34_out, Func2, not_35_out);
  and and_11 (and_11_out, Func5, not_36_out, not_37_out, not_38_out, not_39_out);
  and and_12 (and_12_out, Func5, not_40_out, not_41_out, Func2, not_42_out);
  and and_13 (g, Func5, not_43_out, not_44_out, not_45_out, not_46_out);
  or or_1 (a, and_1_out, and_2_out);
  or or_2 (b, and_3_out, and_4_out);
  or or_3 (c, and_5_out, and_6_out);
  or or_4 (d, and_7_out, and_8_out);
  or or_5 (e, and_9_out, and_10_out);
  or or_6 (f, and_11_out, and_12_out);
endmodule

module display2_controller (
  input  Op5,
  input  Op4,
  input  Op3,
  input  Op2,
  input  Op1,
  input  Op0,
  input  Func5,
  input  Func4,
  input  Func3,
  input  Func2,
  input  Func1,
  input  Func0,
  output a,
  output b,
  output c,
  output d,
  output e,
  output f,
  output g
);

  wire display2_norinstruction_1_a, display2_norinstruction_1_b, display2_norinstruction_1_c,
       display2_norinstruction_1_d, display2_norinstruction_1_e, display2_norinstruction_1_f,
       display2_norinstruction_1_g, display2_rinstruction_1_a, display2_rinstruction_1_b,
       display2_rinstruction_1_c, display2_rinstruction_1_d, display2_rinstruction_1_e,
       display2_rinstruction_1_f, display2_rinstruction_1_g, not_1_out, or_1_out;

  or or_1 (or_1_out, Op0, Op1, Op2, Op3, Op4, Op5);
  display2_noRinstruction display2_norinstruction_1 (
    .Op5(Op5), .Op4(Op4), .Op3(Op3), .Op2(Op2), .Op1(Op1), .Op0(Op0), .Enable(or_1_out),
    .a(display2_norinstruction_1_a), .b(display2_norinstruction_1_b), .c(display2_norinstruction_1_c),
    .d(display2_norinstruction_1_d), .e(display2_norinstruction_1_e), .f(display2_norinstruction_1_f),
    .g(display2_norinstruction_1_g));
  not not_1 (not_1_out, or_1_out);
  display2_Rinstruction display2_rinstruction_1 (
    .Func5(Func5), .Func4(Func4), .Func3(Func3), .Func2(Func2), .Func1(Func1), .Func0(Func0),
    .Enable(not_1_out), .a(display2_rinstruction_1_a), .b(display2_rinstruction_1_b),
    .c(display2_rinstruction_1_c), .d(display2_rinstruction_1_d), .e(display2_rinstruction_1_e),
    .f(display2_rinstruction_1_f), .g(display2_rinstruction_1_g));
  or or_2 (a, display2_norinstruction_1_a, display2_rinstruction_1_a);
  or or_3 (b, display2_norinstruction_1_b, display2_rinstruction_1_b);
  or or_4 (c, display2_norinstruction_1_c, display2_rinstruction_1_c);
  or or_5 (d, display2_norinstruction_1_d, display2_rinstruction_1_d);
  or or_6 (e, display2_norinstruction_1_e, display2_rinstruction_1_e);
  or or_7 (f, display2_norinstruction_1_f, display2_rinstruction_1_f);
  or or_8 (g, display2_norinstruction_1_g, display2_rinstruction_1_g);
endmodule

module display2_noRinstruction (
  input  Op5,
  input  Op4,
  input  Op3,
  input  Op2,
  input  Op1,
  input  Op0,
  input  Enable,
  output a,
  output b,
  output c,
  output d,
  output e,
  output f,
  output g
);

  wire display2_norinstruction_inside_1_a, display2_norinstruction_inside_1_b,
       display2_norinstruction_inside_1_c, display2_norinstruction_inside_1_d,
       display2_norinstruction_inside_1_e, display2_norinstruction_inside_1_f,
       display2_norinstruction_inside_1_g;

  display2_noRinstruction_inside display2_norinstruction_inside_1 (
    .Op5(Op5), .Op4(Op4), .Op3(Op3), .Op2(Op2), .Op1(Op1), .Op0(Op0), .a(display2_norinstruction_inside_1_a),
    .b(display2_norinstruction_inside_1_b), .c(display2_norinstruction_inside_1_c),
    .d(display2_norinstruction_inside_1_d), .e(display2_norinstruction_inside_1_e),
    .f(display2_norinstruction_inside_1_f), .g(display2_norinstruction_inside_1_g));
  and and_1 (a, display2_norinstruction_inside_1_a, Enable);
  and and_2 (b, display2_norinstruction_inside_1_b, Enable);
  and and_3 (c, display2_norinstruction_inside_1_c, Enable);
  and and_4 (d, display2_norinstruction_inside_1_d, Enable);
  and and_5 (e, display2_norinstruction_inside_1_e, Enable);
  and and_6 (f, display2_norinstruction_inside_1_f, Enable);
  and and_7 (g, display2_norinstruction_inside_1_g, Enable);
endmodule

module display2_Rinstruction (
  input  Func5,
  input  Func4,
  input  Func3,
  input  Func2,
  input  Func1,
  input  Func0,
  input  Enable,
  output a,
  output b,
  output c,
  output d,
  output e,
  output f,
  output g
);

  wire display2_rinstruction_inside_1_a, display2_rinstruction_inside_1_b, display2_rinstruction_inside_1_c,
       display2_rinstruction_inside_1_d, display2_rinstruction_inside_1_e, display2_rinstruction_inside_1_f,
       display2_rinstruction_inside_1_g;

  display2_Rinstruction_inside display2_rinstruction_inside_1 (
    .Func5(Func5), .Func4(Func4), .Func3(Func3), .Func2(Func2), .Func1(Func1), .Func0(Func0),
    .a(display2_rinstruction_inside_1_a), .b(display2_rinstruction_inside_1_b),
    .c(display2_rinstruction_inside_1_c), .d(display2_rinstruction_inside_1_d),
    .e(display2_rinstruction_inside_1_e), .f(display2_rinstruction_inside_1_f),
    .g(display2_rinstruction_inside_1_g));
  and and_1 (a, display2_rinstruction_inside_1_a, Enable);
  and and_2 (b, display2_rinstruction_inside_1_b, Enable);
  and and_3 (c, display2_rinstruction_inside_1_c, Enable);
  and and_4 (d, display2_rinstruction_inside_1_d, Enable);
  and and_5 (e, display2_rinstruction_inside_1_e, Enable);
  and and_6 (f, display2_rinstruction_inside_1_f, Enable);
  and and_7 (g, display2_rinstruction_inside_1_g, Enable);
endmodule

module display2_noRinstruction_inside (
  input  Op5,
  input  Op4,
  input  Op3,
  input  Op2,
  input  Op1,
  input  Op0,
  output a,
  output b,
  output c,
  output d,
  output e,
  output f,
  output g
);

  wire and_1_out, and_2_out, and_3_out, and_4_out, and_5_out, and_6_out, and_7_out, and_8_out, and_9_out,
       and_10_out, and_11_out, and_12_out, and_13_out, and_14_out, and_15_out, and_16_out, and_17_out,
       and_18_out, and_19_out, and_20_out, and_21_out, and_22_out, not_1_out, not_2_out, not_3_out,
       not_4_out, not_5_out, not_6_out, not_7_out, not_8_out, not_9_out, not_10_out, not_11_out, not_12_out,
       not_13_out, not_14_out, not_15_out, not_16_out, not_17_out, not_18_out, not_19_out, not_20_out,
       not_21_out, not_22_out, not_23_out, not_24_out, not_25_out, not_26_out, not_27_out, not_28_out,
       not_29_out, not_30_out, not_31_out, not_32_out, not_33_out, not_34_out, not_35_out, not_36_out,
       not_37_out, not_38_out, not_39_out, not_40_out, not_41_out, not_42_out, not_43_out, not_44_out,
       not_45_out, not_46_out, not_47_out, not_48_out, not_49_out, not_50_out, not_51_out, not_52_out,
       not_53_out, not_54_out, not_55_out, not_56_out, not_57_out, not_58_out, not_59_out, not_60_out,
       not_61_out, not_62_out, not_63_out, not_64_out, not_65_out, not_66_out, not_67_out, not_68_out,
       not_69_out, not_70_out, not_71_out, not_72_out, not_73_out, not_74_out, not_75_out, not_76_out,
       not_77_out, not_78_out, not_79_out, not_80_out, not_81_out, not_82_out, not_83_out, not_84_out,
       not_85_out, not_86_out, not_87_out, not_88_out, not_89_out, not_90_out, not_91_out, not_92_out;

  not not_1 (not_1_out, Op5);
  not not_2 (not_2_out, Op4);
  not not_3 (not_3_out, Op3);
  not not_4 (not_4_out, Op1);
  not not_5 (not_5_out, Op0);
  not not_6 (not_6_out, Op4);
  not not_7 (not_7_out, Op3);
  not not_8 (not_8_out, Op2);
  not not_9 (not_9_out, Op5);
  not not_10 (not_10_out, Op4);
  not not_11 (not_11_out, Op3);
  not not_12 (not_12_out, Op2);
  not not_13 (not_13_out, Op0);
  not not_14 (not_14_out, Op5);
  not not_15 (not_15_out, Op4);
  not not_16 (not_16_out, Op2);
  not not_17 (not_17_out, Op1);
  not not_18 (not_18_out, Op0);
  not not_19 (not_19_out, Op4);
  not not_20 (not_20_out, Op3);
  not not_21 (not_21_out, Op2);
  not not_22 (not_22_out, Op5);
  not not_23 (not_23_out, Op4);
  not not_24 (not_24_out, Op3);
  not not_25 (not_25_out, Op2);
  not not_26 (not_26_out, Op0);
  not not_27 (not_27_out, Op5);
  not not_28 (not_28_out, Op4);
  not not_29 (not_29_out, Op2);
  not not_30 (not_30_out, Op1);
  not not_31 (not_31_out, Op0);
  not not_32 (not_32_out, Op4);
  not not_33 (not_33_out, Op3);
  not not_34 (not_34_out, Op2);
  not not_35 (not_35_out, Op5);
  not not_36 (not_36_out, Op4);
  not not_37 (not_37_out, Op3);
  not not_38 (not_38_out, Op2);
  not not_39 (not_39_out, Op0);
  not not_40 (not_40_out, Op5);
  not not_41 (not_41_out, Op4);
  not not_42 (not_42_out, Op3);
  not not_43 (not_43_out, Op1);
  not not_44 (not_44_out, Op0);
  not not_45 (not_45_out, Op5);
  not not_46 (not_46_out, Op4);
  not not_47 (not_47_out, Op2);
  not not_48 (not_48_out, Op1);
  not not_49 (not_49_out, Op0);
  not not_50 (not_50_out, Op4);
  not not_51 (not_51_out, Op2);
  not not_52 (not_52_out, Op5);
  not not_53 (not_53_out, Op4);
  not not_54 (not_54_out, Op3);
  not not_55 (not_55_out, Op2);
  not not_56 (not_56_out, Op0);
  not not_57 (not_57_out, Op5);
  not not_58 (not_58_out, Op4);
  not not_59 (not_59_out, Op3);
  not not_60 (not_60_out, Op1);
  not not_61 (not_61_out, Op0);
  not not_62 (not_62_out, Op5);
  not not_63 (not_63_out, Op4);
  not not_64 (not_64_out, Op2);
  not not_65 (not_65_out, Op1);
  not not_66 (not_66_out, Op0);
  not not_67 (not_67_out, Op4);
  not not_68 (not_68_out, Op2);
  not not_69 (not_69_out, Op5);
  not not_70 (not_70_out, Op4);
  not not_71 (not_71_out, Op3);
  not not_72 (not_72_out, Op2);
  not not_73 (not_73_out, Op0);
  not not_74 (not_74_out, Op5);
  not not_75 (not_75_out, Op4);
  not not_76 (not_76_out, Op3);
  not not_77 (not_77_out, Op1);
  not not_78 (not_78_out, Op0);
  not not_79 (not_79_out, Op4);
  not not_80 (not_80_out, Op2);
  not not_81 (not_81_out, Op5);
  not not_82 (not_82_out, Op4);
  not not_83 (not_83_out, Op3);
  not not_84 (not_84_out, Op1);
  not not_85 (not_85_out, Op0);
  not not_86 (not_86_out, Op5);
  not not_87 (not_87_out, Op4);
  not not_88 (not_88_out, Op2);
  not not_89 (not_89_out, Op1);
  not not_90 (not_90_out, Op0);
  not not_91 (not_91_out, Op4);
  not not_92 (not_92_out, Op2);
  and and_1 (and_1_out, not_1_out, not_2_out, not_3_out, Op2, not_4_out, not_5_out);
  and and_2 (and_2_out, Op5, not_6_out, not_7_out, not_8_out, Op1, Op0);
  and and_3 (and_3_out, not_9_out, not_10_out, not_11_out, not_12_out, Op1, not_13_out);
  and and_4 (and_4_out, not_14_out, not_15_out, Op3, not_16_out, not_17_out, not_18_out);
  and and_5 (and_5_out, Op5, not_19_out, not_20_out, not_21_out, Op1, Op0);
  and and_6 (and_6_out, not_22_out, not_23_out, not_24_out, not_25_out, Op1, not_26_out);
  and and_7 (and_7_out, not_27_out, not_28_out, Op3, not_29_out, not_30_out, not_31_out);
  and and_8 (and_8_out, Op5, not_32_out, not_33_out, not_34_out, Op1, Op0);
  and and_9 (and_9_out, not_35_out, not_36_out, not_37_out, not_38_out, Op1, not_39_out);
  and and_10 (and_10_out, not_40_out, not_41_out, not_42_out, Op2, not_43_out, not_44_out);
  and and_11 (and_11_out, not_45_out, not_46_out, Op3, not_47_out, not_48_out, not_49_out);
  and and_12 (and_12_out, Op5, not_50_out, not_51_out, Op1, Op0);
  and and_13 (and_13_out, not_52_out, not_53_out, not_54_out, not_55_out, Op1, not_56_out);
  and and_14 (and_14_out, not_57_out, not_58_out, not_59_out, Op2, not_60_out, not_61_out);
  and and_15 (and_15_out, not_62_out, not_63_out, Op3, not_64_out, not_65_out, not_66_out);
  and and_16 (and_16_out, Op5, not_67_out, not_68_out, Op1, Op0);
  and and_17 (and_17_out, not_69_out, not_70_out, not_71_out, not_72_out, Op1, not_73_out);
  and and_18 (and_18_out, not_74_out, not_75_out, not_76_out, Op2, not_77_out, not_78_out);
  and and_19 (and_19_out, Op5, not_79_out, not_80_out, Op1, Op0);
  and and_20 (and_20_out, not_81_out, not_82_out, not_83_out, Op2, not_84_out, not_85_out);
  and and_21 (and_21_out, not_86_out, not_87_out, Op3, not_88_out, not_89_out, not_90_out);
  and and_22 (and_22_out, Op5, not_91_out, Op3, not_92_out, Op1, Op0);
  or or_1 (a, and_1_out, and_2_out);
  or or_2 (b, and_3_out, and_4_out, and_5_out);
  or or_3 (c, and_6_out, and_7_out, and_8_out);
  or or_4 (d, and_9_out, and_10_out, and_11_out, and_12_out);
  or or_5 (e, and_13_out, and_14_out, and_15_out, and_16_out);
  or or_6 (f, and_17_out, and_18_out, and_19_out);
  or or_7 (g, and_20_out, and_21_out, and_22_out);
endmodule

module display2_Rinstruction_inside (
  input  Func5,
  input  Func4,
  input  Func3,
  input  Func2,
  input  Func1,
  input  Func0,
  output a,
  output b,
  output c,
  output d,
  output e,
  output f,
  output g
);

  wire and_2_out, and_3_out, and_4_out, and_5_out, and_7_out, and_8_out, and_9_out, and_10_out, not_1_out,
       not_2_out, not_3_out, not_4_out, not_5_out, not_6_out, not_7_out, not_8_out, not_9_out, not_10_out,
       not_11_out, not_12_out, not_13_out, not_14_out, not_15_out, not_16_out, not_17_out, not_18_out,
       not_19_out, not_20_out, not_21_out, not_22_out, not_23_out, not_24_out, not_25_out, not_26_out,
       not_27_out, not_28_out, not_29_out, not_30_out, not_31_out, not_32_out, not_33_out, not_34_out,
       not_35_out, not_36_out, not_37_out, not_38_out, not_39_out, not_40_out, not_41_out, not_42_out;

  not not_1 (not_1_out, Func4);
  not not_2 (not_2_out, Func3);
  not not_3 (not_3_out, Func1);
  not not_4 (not_4_out, Func4);
  not not_5 (not_5_out, Func3);
  not not_6 (not_6_out, Func2);
  not not_7 (not_7_out, Func0);
  not not_8 (not_8_out, Func4);
  not not_9 (not_9_out, Func3);
  not not_10 (not_10_out, Func1);
  not not_11 (not_11_out, Func0);
  not not_12 (not_12_out, Func4);
  not not_13 (not_13_out, Func3);
  not not_14 (not_14_out, Func2);
  not not_15 (not_15_out, Func0);
  not not_16 (not_16_out, Func4);
  not not_17 (not_17_out, Func3);
  not not_18 (not_18_out, Func1);
  not not_19 (not_19_out, Func0);
  not not_20 (not_20_out, Func4);
  not not_21 (not_21_out, Func3);
  not not_22 (not_22_out, Func2);
  not not_23 (not_23_out, Func0);
  not not_24 (not_24_out, Func4);
  not not_25 (not_25_out, Func3);
  not not_26 (not_26_out, Func2);
  not not_27 (not_27_out, Func0);
  not not_28 (not_28_out, Func4);
  not not_29 (not_29_out, Func3);
  not not_30 (not_30_out, Func1);
  not not_31 (not_31_out, Func4);
  not not_32 (not_32_out, Func3);
  not not_33 (not_33_out, Func2);
  not not_34 (not_34_out, Func0);
  not not_35 (not_35_out, Func4);
  not not_36 (not_36_out, Func3);
  not not_37 (not_37_out, Func1);
  not not_38 (not_38_out, Func4);
  not not_39 (not_39_out, Func3);
  not not_40 (not_40_out, Func2);
  not not_41 (not_41_out, Func1);
  not not_42 (not_42_out, Func0);
  and and_1 (a, Func5, not_1_out, not_2_out, Func2, not_3_out);
  and and_2 (and_2_out, Func5, not_4_out, not_5_out, not_6_out, not_7_out);
  and and_3 (and_3_out, Func5, not_8_out, not_9_out, not_10_out, not_11_out);
  and and_4 (and_4_out, Func5, not_12_out, not_13_out, not_14_out, not_15_out);
  and and_5 (and_5_out, Func5, not_16_out, not_17_out, not_18_out, not_19_out);
  and and_6 (d, Func5, not_20_out, not_21_out, not_22_out, not_23_out);
  and and_7 (and_7_out, Func5, not_24_out, not_25_out, not_26_out, not_27_out);
  and and_8 (and_8_out, Func5, not_28_out, not_29_out, Func2, not_30_out);
  and and_9 (and_9_out, Func5, not_31_out, not_32_out, not_33_out, Func1, not_34_out);
  and and_10 (and_10_out, Func5, not_35_out, not_36_out, Func2, not_37_out);
  and and_11 (g, Func5, not_38_out, not_39_out, not_40_out, not_41_out, not_42_out);
  or or_1 (b, and_2_out, and_3_out);
  or or_2 (c, and_4_out, and_5_out);
  or or_3 (e, and_7_out, and_8_out);
  or or_4 (f, and_9_out, and_10_out);
endmodule

module display3_controller (
  input  Op5,
  input  Op4,
  input  Op3,
  input  Op2,
  input  Op1,
  input  Op0,
  input  Func5,
  input  Func4,
  input  Func3,
  input  Func2,
  input  Func1,
  input  Func0,
  output a,
  output b,
  output c,
  output d,
  output e,
  output f,
  output g
);

  wire display3_norinstruction_1_a, display3_norinstruction_1_b, display3_norinstruction_1_c,
       display3_norinstruction_1_d, display3_norinstruction_1_e, display3_norinstruction_1_f,
       display3_norinstruction_1_g, display3_rinstruction_1_a, display3_rinstruction_1_b,
       display3_rinstruction_1_c, display3_rinstruction_1_d, display3_rinstruction_1_e,
       display3_rinstruction_1_f, display3_rinstruction_1_g, not_1_out, or_1_out;

  or or_1 (or_1_out, Op0, Op1, Op2, Op3, Op4, Op5);
  display3_noRinstruction display3_norinstruction_1 (
    .Op5(Op5), .Op4(Op4), .Op3(Op3), .Op2(Op2), .Op1(Op1), .Op0(Op0), .Enable(or_1_out),
    .a(display3_norinstruction_1_a), .b(display3_norinstruction_1_b), .c(display3_norinstruction_1_c),
    .d(display3_norinstruction_1_d), .e(display3_norinstruction_1_e), .f(display3_norinstruction_1_f),
    .g(display3_norinstruction_1_g));
  not not_1 (not_1_out, or_1_out);
  display3_Rinstruction display3_rinstruction_1 (
    .Func5(Func5), .Func4(Func4), .Func3(Func3), .Func2(Func2), .Func1(Func1), .Func0(Func0),
    .Enable(not_1_out), .a(display3_rinstruction_1_a), .b(display3_rinstruction_1_b),
    .c(display3_rinstruction_1_c), .d(display3_rinstruction_1_d), .e(display3_rinstruction_1_e),
    .f(display3_rinstruction_1_f), .g(display3_rinstruction_1_g));
  or or_2 (a, display3_norinstruction_1_a, display3_rinstruction_1_a);
  or or_3 (b, display3_norinstruction_1_b, display3_rinstruction_1_b);
  or or_4 (c, display3_norinstruction_1_c, display3_rinstruction_1_c);
  or or_5 (d, display3_norinstruction_1_d, display3_rinstruction_1_d);
  or or_6 (e, display3_norinstruction_1_e, display3_rinstruction_1_e);
  or or_7 (f, display3_norinstruction_1_f, display3_rinstruction_1_f);
  or or_8 (g, display3_norinstruction_1_g, display3_rinstruction_1_g);
endmodule

module display3_noRinstruction (
  input  Op5,
  input  Op4,
  input  Op3,
  input  Op2,
  input  Op1,
  input  Op0,
  input  Enable,
  output a,
  output b,
  output c,
  output d,
  output e,
  output f,
  output g
);

  wire display3_norinstruction_inside_1_a, display3_norinstruction_inside_1_b,
       display3_norinstruction_inside_1_c, display3_norinstruction_inside_1_d,
       display3_norinstruction_inside_1_e, display3_norinstruction_inside_1_f,
       display3_norinstruction_inside_1_g;

  display3_noRinstruction_inside display3_norinstruction_inside_1 (
    .Op5(Op5), .Op4(Op4), .Op3(Op3), .Op2(Op2), .Op1(Op1), .Op0(Op0), .a(display3_norinstruction_inside_1_a),
    .b(display3_norinstruction_inside_1_b), .c(display3_norinstruction_inside_1_c),
    .d(display3_norinstruction_inside_1_d), .e(display3_norinstruction_inside_1_e),
    .f(display3_norinstruction_inside_1_f), .g(display3_norinstruction_inside_1_g));
  and and_1 (a, display3_norinstruction_inside_1_a, Enable);
  and and_2 (b, display3_norinstruction_inside_1_b, Enable);
  and and_3 (c, display3_norinstruction_inside_1_c, Enable);
  and and_4 (d, display3_norinstruction_inside_1_d, Enable);
  and and_5 (e, display3_norinstruction_inside_1_e, Enable);
  and and_6 (f, display3_norinstruction_inside_1_f, Enable);
  and and_7 (g, display3_norinstruction_inside_1_g, Enable);
endmodule

module display3_Rinstruction (
  input  Func5,
  input  Func4,
  input  Func3,
  input  Func2,
  input  Func1,
  input  Func0,
  input  Enable,
  output a,
  output b,
  output c,
  output d,
  output e,
  output f,
  output g
);

  wire display3_rinstruction_inside_1_a, display3_rinstruction_inside_1_b, display3_rinstruction_inside_1_c,
       display3_rinstruction_inside_1_d, display3_rinstruction_inside_1_e, display3_rinstruction_inside_1_f,
       display3_rinstruction_inside_1_g;

  display3_Rinstruction_inside display3_rinstruction_inside_1 (
    .Func5(Func5), .a(display3_rinstruction_inside_1_a), .Func4(Func4), .b(display3_rinstruction_inside_1_b),
    .Func3(Func3), .Func2(Func2), .Func1(Func1), .Func0(Func0), .c(display3_rinstruction_inside_1_c),
    .d(display3_rinstruction_inside_1_d), .e(display3_rinstruction_inside_1_e),
    .f(display3_rinstruction_inside_1_f), .g(display3_rinstruction_inside_1_g));
  and and_1 (a, display3_rinstruction_inside_1_a, Enable);
  and and_2 (b, display3_rinstruction_inside_1_b, Enable);
  and and_3 (c, display3_rinstruction_inside_1_c, Enable);
  and and_4 (d, display3_rinstruction_inside_1_d, Enable);
  and and_5 (e, display3_rinstruction_inside_1_e, Enable);
  and and_6 (f, display3_rinstruction_inside_1_f, Enable);
  and and_7 (g, display3_rinstruction_inside_1_g, Enable);
endmodule

module display3_noRinstruction_inside (
  input  Op5,
  input  Op4,
  input  Op3,
  input  Op2,
  input  Op1,
  input  Op0,
  output a,
  output b,
  output c,
  output d,
  output e,
  output f,
  output g
);

  wire and_1_out, and_2_out, and_3_out, and_4_out, and_5_out, and_6_out, and_7_out, and_8_out, and_9_out,
       and_11_out, and_12_out, and_13_out, and_14_out, and_15_out, and_16_out, and_17_out, and_18_out,
       and_19_out, not_1_out, not_2_out, not_3_out, not_4_out, not_5_out, not_6_out, not_7_out, not_8_out,
       not_9_out, not_10_out, not_11_out, not_12_out, not_13_out, not_14_out, not_15_out, not_16_out,
       not_17_out, not_18_out, not_19_out, not_20_out, not_21_out, not_22_out, not_23_out, not_24_out,
       not_25_out, not_26_out, not_27_out, not_28_out, not_29_out, not_30_out, not_31_out, not_32_out,
       not_33_out, not_34_out, not_35_out, not_36_out, not_37_out, not_38_out, not_39_out, not_40_out,
       not_41_out, not_42_out, not_43_out, not_44_out, not_45_out, not_46_out, not_47_out, not_48_out,
       not_49_out, not_50_out, not_51_out, not_52_out, not_53_out, not_54_out, not_55_out, not_56_out,
       not_57_out, not_58_out, not_59_out, not_60_out, not_61_out, not_62_out, not_63_out, not_64_out,
       not_65_out, not_66_out, not_67_out, not_68_out, not_69_out, not_70_out, not_71_out, not_72_out,
       not_73_out, not_74_out, not_75_out, not_76_out, not_77_out, not_78_out, not_79_out, not_80_out;

  not not_1 (not_1_out, Op5);
  not not_2 (not_2_out, Op4);
  not not_3 (not_3_out, Op3);
  not not_4 (not_4_out, Op1);
  not not_5 (not_5_out, Op0);
  not not_6 (not_6_out, Op4);
  not not_7 (not_7_out, Op2);
  not not_8 (not_8_out, Op5);
  not not_9 (not_9_out, Op4);
  not not_10 (not_10_out, Op3);
  not not_11 (not_11_out, Op1);
  not not_12 (not_12_out, Op0);
  not not_13 (not_13_out, Op5);
  not not_14 (not_14_out, Op4);
  not not_15 (not_15_out, Op2);
  not not_16 (not_16_out, Op1);
  not not_17 (not_17_out, Op0);
  not not_18 (not_18_out, Op4);
  not not_19 (not_19_out, Op3);
  not not_20 (not_20_out, Op2);
  not not_21 (not_21_out, Op5);
  not not_22 (not_22_out, Op4);
  not not_23 (not_23_out, Op3);
  not not_24 (not_24_out, Op2);
  not not_25 (not_25_out, Op0);
  not not_26 (not_26_out, Op5);
  not not_27 (not_27_out, Op4);
  not not_28 (not_28_out, Op3);
  not not_29 (not_29_out, Op1);
  not not_30 (not_30_out, Op0);
  not not_31 (not_31_out, Op5);
  not not_32 (not_32_out, Op4);
  not not_33 (not_33_out, Op2);
  not not_34 (not_34_out, Op1);
  not not_35 (not_35_out, Op0);
  not not_36 (not_36_out, Op4);
  not not_37 (not_37_out, Op3);
  not not_38 (not_38_out, Op2);
  not not_39 (not_39_out, Op5);
  not not_40 (not_40_out, Op4);
  not not_41 (not_41_out, Op2);
  not not_42 (not_42_out, Op1);
  not not_43 (not_43_out, Op0);
  not not_44 (not_44_out, Op5);
  not not_45 (not_45_out, Op4);
  not not_46 (not_46_out, Op3);
  not not_47 (not_47_out, Op2);
  not not_48 (not_48_out, Op0);
  not not_49 (not_49_out, Op5);
  not not_50 (not_50_out, Op4);
  not not_51 (not_51_out, Op2);
  not not_52 (not_52_out, Op1);
  not not_53 (not_53_out, Op0);
  not not_54 (not_54_out, Op4);
  not not_55 (not_55_out, Op2);
  not not_56 (not_56_out, Op5);
  not not_57 (not_57_out, Op4);
  not not_58 (not_58_out, Op3);
  not not_59 (not_59_out, Op1);
  not not_60 (not_60_out, Op0);
  not not_61 (not_61_out, Op4);
  not not_62 (not_62_out, Op2);
  not not_63 (not_63_out, Op5);
  not not_64 (not_64_out, Op4);
  not not_65 (not_65_out, Op3);
  not not_66 (not_66_out, Op2);
  not not_67 (not_67_out, Op0);
  not not_68 (not_68_out, Op5);
  not not_69 (not_69_out, Op4);
  not not_70 (not_70_out, Op3);
  not not_71 (not_71_out, Op1);
  not not_72 (not_72_out, Op0);
  not not_73 (not_73_out, Op5);
  not not_74 (not_74_out, Op4);
  not not_75 (not_75_out, Op2);
  not not_76 (not_76_out, Op1);
  not not_77 (not_77_out, Op0);
  not not_78 (not_78_out, Op4);
  not not_79 (not_79_out, Op3);
  not not_80 (not_80_out, Op2);
  and and_1 (and_1_out, not_1_out, not_2_out, not_3_out, Op2, not_4_out, not_5_out);
  and and_2 (and_2_out, Op5, not_6_out, not_7_out, Op1, Op0);
  and and_3 (and_3_out, not_8_out, not_9_out, not_10_out, Op2, not_11_out, not_12_out);
  and and_4 (and_4_out, not_13_out, not_14_out, Op3, not_15_out, not_16_out, not_17_out);
  and and_5 (and_5_out, Op5, not_18_out, not_19_out, not_20_out, Op1, Op0);
  and and_6 (and_6_out, not_21_out, not_22_out, not_23_out, not_24_out, Op1, not_25_out);
  and and_7 (and_7_out, not_26_out, not_27_out, not_28_out, Op2, not_29_out, not_30_out);
  and and_8 (and_8_out, not_31_out, not_32_out, Op3, not_33_out, not_34_out, not_35_out);
  and and_9 (and_9_out, Op5, not_36_out, not_37_out, not_38_out, Op1, Op0);
  and and_10 (d, not_39_out, not_40_out, Op3, not_41_out, not_42_out, not_43_out);
  and and_11 (and_11_out, not_44_out, not_45_out, not_46_out, not_47_out, Op1, not_48_out);
  and and_12 (and_12_out, not_49_out, not_50_out, Op3, not_51_out, not_52_out, not_53_out);
  and and_13 (and_13_out, Op5, not_54_out, not_55_out, Op1, Op0);
  and and_14 (and_14_out, not_56_out, not_57_out, not_58_out, Op2, not_59_out, not_60_out);
  and and_15 (and_15_out, Op5, not_61_out, not_62_out, Op1, Op0);
  and and_16 (and_16_out, not_63_out, not_64_out, not_65_out, not_66_out, Op1, not_67_out);
  and and_17 (and_17_out, not_68_out, not_69_out, not_70_out, Op2, not_71_out, not_72_out);
  and and_18 (and_18_out, not_73_out, not_74_out, Op3, not_75_out, not_76_out, not_77_out);
  and and_19 (and_19_out, Op5, not_78_out, not_79_out, not_80_out, Op1, Op0);
  or or_1 (a, and_1_out, and_2_out);
  or or_2 (b, and_3_out, and_4_out, and_5_out);
  or or_3 (c, and_6_out, and_7_out, and_8_out, and_9_out);
  or or_4 (e, and_11_out, and_12_out, and_13_out);
  or or_5 (f, and_14_out, and_15_out);
  or or_6 (g, and_16_out, and_17_out, and_18_out, and_19_out);
endmodule
module display3_Rinstruction_inside (
  input  Func5,
  input  Func4,
  input  Func3,
  input  Func2,
  input  Func1,
  input  Func0,
  output a,
  output b,
  output c,
  output d,
  output e,
  output f,
  output g
);

  wire and_2_out, and_3_out, and_4_out, and_5_out, and_6_out, and_7_out, and_9_out, and_10_out, not_1_out,
       not_2_out, not_3_out, not_4_out, not_5_out, not_6_out, not_7_out, not_8_out, not_9_out, not_10_out,
       not_11_out, not_12_out, not_13_out, not_14_out, not_15_out, not_16_out, not_17_out, not_18_out,
       not_19_out, not_20_out, not_21_out, not_22_out, not_23_out, not_24_out, not_25_out, not_26_out,
       not_27_out, not_28_out, not_29_out, not_30_out, not_31_out, not_32_out, not_33_out, not_34_out,
       not_35_out, not_36_out, not_37_out, not_38_out, not_39_out, not_40_out;

  not not_1 (not_1_out, Func4);
  not not_2 (not_2_out, Func3);
  not not_3 (not_3_out, Func1);
  not not_4 (not_4_out, Func0);
  not not_5 (not_5_out, Func4);
  not not_6 (not_6_out, Func3);
  not not_7 (not_7_out, Func2);
  not not_8 (not_8_out, Func0);
  not not_9 (not_9_out, Func4);
  not not_10 (not_10_out, Func3);
  not not_11 (not_11_out, Func1);
  not not_12 (not_12_out, Func0);
  not not_13 (not_13_out, Func4);
  not not_14 (not_14_out, Func3);
  not not_15 (not_15_out, Func2);
  not not_16 (not_16_out, Func0);
  not not_17 (not_17_out, Func4);
  not not_18 (not_18_out, Func3);
  not not_19 (not_19_out, Func1);
  not not_20 (not_20_out, Func0);
  not not_21 (not_21_out, Func4);
  not not_22 (not_22_out, Func3);
  not not_23 (not_23_out, Func2);
  not not_24 (not_24_out, Func0);
  not not_25 (not_25_out, Func4);
  not not_26 (not_26_out, Func3);
  not not_27 (not_27_out, Func1);
  not not_28 (not_28_out, Func0);
  not not_29 (not_29_out, Func4);
  not not_30 (not_30_out, Func3);
  not not_31 (not_31_out, Func2);
  not not_32 (not_32_out, Func0);
  not not_33 (not_33_out, Func4);
  not not_34 (not_34_out, Func3);
  not not_35 (not_35_out, Func2);
  not not_36 (not_36_out, Func0);
  not not_37 (not_37_out, Func4);
  not not_38 (not_38_out, Func3);
  not not_39 (not_39_out, Func1);
  not not_40 (not_40_out, Func0);
  and and_1 (b, Func5, not_1_out, not_2_out, not_3_out, not_4_out);
  and and_2 (and_2_out, Func5, not_5_out, not_6_out, not_7_out, not_8_out);
  and and_3 (and_3_out, Func5, not_9_out, not_10_out, not_11_out, not_12_out);
  and and_4 (and_4_out, Func5, not_13_out, not_14_out, not_15_out, not_16_out);
  and and_5 (and_5_out, Func5, not_17_out, not_18_out, not_19_out, not_20_out);
  and and_6 (and_6_out, Func5, not_21_out, not_22_out, not_23_out, not_24_out);
  and and_7 (and_7_out, Func5, not_25_out, not_26_out, not_27_out, not_28_out);
  and and_8 (f, Func5, not_29_out, not_30_out, not_31_out, Func1, not_32_out);
  and and_9 (and_9_out, Func5, not_33_out, not_34_out, not_35_out, not_36_out);
  and and_10 (and_10_out, Func5, not_37_out, not_38_out, not_39_out, not_40_out);
  or or_1 (c, and_2_out, and_3_out);
  or or_2 (d, and_4_out, and_5_out);
  or or_3 (e, and_6_out, and_7_out);
  or or_4 (g, and_9_out, and_10_out);

  assign a = 1'b0;
endmodule

module display4_controller (
  input  Op5,
  input  Op4,
  input  Op3,
  input  Op2,
  input  Op1,
  input  Op0,
  input  Func5,
  input  Func4,
  input  Func3,
  input  Func2,
  input  Func1,
  input  Func0,
  output a,
  output b,
  output c,
  output d,
  output e,
  output f,
  output g
);

  wire display4_norinstruction_1_a, display4_norinstruction_1_b, display4_norinstruction_1_c,
       display4_norinstruction_1_d, display4_norinstruction_1_e, display4_norinstruction_1_f,
       display4_norinstruction_1_g, display4_rinstruction_1_a, display4_rinstruction_1_b,
       display4_rinstruction_1_c, display4_rinstruction_1_d, display4_rinstruction_1_e,
       display4_rinstruction_1_f, display4_rinstruction_1_g, not_1_out, or_1_out;

  or or_1 (or_1_out, Op0, Op1, Op2, Op3, Op4, Op5);
  display4_noRinstruction display4_norinstruction_1 (
    .Op5(Op5), .Op4(Op4), .Op3(Op3), .Op2(Op2), .Op1(Op1), .Op0(Op0), .Enable(or_1_out),
    .a(display4_norinstruction_1_a), .b(display4_norinstruction_1_b), .c(display4_norinstruction_1_c),
    .d(display4_norinstruction_1_d), .e(display4_norinstruction_1_e), .f(display4_norinstruction_1_f),
    .g(display4_norinstruction_1_g));
  not not_1 (not_1_out, or_1_out);
  display4_Rinstruction display4_rinstruction_1 (
    .Func5(Func5), .Func4(Func4), .Func3(Func3), .Func2(Func2), .Func1(Func1), .Func0(Func0),
    .Enable(not_1_out), .a(display4_rinstruction_1_a), .b(display4_rinstruction_1_b),
    .c(display4_rinstruction_1_c), .d(display4_rinstruction_1_d), .e(display4_rinstruction_1_e),
    .f(display4_rinstruction_1_f), .g(display4_rinstruction_1_g));
  or or_2 (a, display4_norinstruction_1_a, display4_rinstruction_1_a);
  or or_3 (b, display4_norinstruction_1_b, display4_rinstruction_1_b);
  or or_4 (c, display4_norinstruction_1_c, display4_rinstruction_1_c);
  or or_5 (d, display4_norinstruction_1_d, display4_rinstruction_1_d);
  or or_6 (e, display4_norinstruction_1_e, display4_rinstruction_1_e);
  or or_7 (f, display4_norinstruction_1_f, display4_rinstruction_1_f);
  or or_8 (g, display4_norinstruction_1_g, display4_rinstruction_1_g);
endmodule

module display4_noRinstruction (
  input  Op5,
  input  Op4,
  input  Op3,
  input  Op2,
  input  Op1,
  input  Op0,
  input  Enable,
  output a,
  output b,
  output c,
  output d,
  output e,
  output f,
  output g
);

  wire display4_norinstruction_inside_1_a, display4_norinstruction_inside_1_b,
       display4_norinstruction_inside_1_c, display4_norinstruction_inside_1_d,
       display4_norinstruction_inside_1_e, display4_norinstruction_inside_1_f,
       display4_norinstruction_inside_1_g;

  display4_noRinstruction_inside display4_norinstruction_inside_1 (
    .Op5(Op5), .Op4(Op4), .Op3(Op3), .Op2(Op2), .Op1(Op1), .Op0(Op0), .a(display4_norinstruction_inside_1_a),
    .b(display4_norinstruction_inside_1_b), .c(display4_norinstruction_inside_1_c),
    .d(display4_norinstruction_inside_1_d), .e(display4_norinstruction_inside_1_e),
    .f(display4_norinstruction_inside_1_f), .g(display4_norinstruction_inside_1_g));
  and and_1 (a, display4_norinstruction_inside_1_a, Enable);
  and and_2 (b, display4_norinstruction_inside_1_b, Enable);
  and and_3 (c, display4_norinstruction_inside_1_c, Enable);
  and and_4 (d, display4_norinstruction_inside_1_d, Enable);
  and and_5 (e, display4_norinstruction_inside_1_e, Enable);
  and and_6 (f, display4_norinstruction_inside_1_f, Enable);
  and and_7 (g, display4_norinstruction_inside_1_g, Enable);
endmodule

module display4_Rinstruction (
  input  Func5,
  input  Func4,
  input  Func3,
  input  Func2,
  input  Func1,
  input  Func0,
  input  Enable,
  output a,
  output b,
  output c,
  output d,
  output e,
  output f,
  output g
);

  wire display4_rinstruction_inside_1_a, display4_rinstruction_inside_1_b, display4_rinstruction_inside_1_c,
       display4_rinstruction_inside_1_d, display4_rinstruction_inside_1_e, display4_rinstruction_inside_1_f,
       display4_rinstruction_inside_1_g;

  display4_Rinstruction_inside display4_rinstruction_inside_1 (
    .Func5(Func5), .Func4(Func4), .Func3(Func3), .Func2(Func2), .Func1(Func1), .Func0(Func0),
    .a(display4_rinstruction_inside_1_a), .b(display4_rinstruction_inside_1_b),
    .c(display4_rinstruction_inside_1_c), .d(display4_rinstruction_inside_1_d),
    .e(display4_rinstruction_inside_1_e), .f(display4_rinstruction_inside_1_f),
    .g(display4_rinstruction_inside_1_g));
  and and_1 (a, display4_rinstruction_inside_1_a, Enable);
  and and_2 (b, display4_rinstruction_inside_1_b, Enable);
  and and_3 (c, display4_rinstruction_inside_1_c, Enable);
  and and_4 (d, display4_rinstruction_inside_1_d, Enable);
  and and_5 (e, display4_rinstruction_inside_1_e, Enable);
  and and_6 (f, display4_rinstruction_inside_1_f, Enable);
  and and_7 (g, display4_rinstruction_inside_1_g, Enable);
endmodule

module display4_noRinstruction_inside (
  input  Op5,
  input  Op4,
  input  Op3,
  input  Op2,
  input  Op1,
  input  Op0,
  output a,
  output b,
  output c,
  output d,
  output e,
  output f,
  output g
);

  wire and_2_out, and_3_out, and_5_out, and_6_out, and_7_out, and_8_out, and_9_out, and_10_out, and_11_out,
       not_1_out, not_2_out, not_3_out, not_4_out, not_5_out, not_6_out, not_7_out, not_8_out, not_9_out,
       not_10_out, not_11_out, not_12_out, not_13_out, not_14_out, not_15_out, not_16_out, not_17_out,
       not_18_out, not_19_out, not_20_out, not_21_out, not_22_out, not_23_out, not_24_out, not_25_out,
       not_26_out, not_27_out, not_28_out, not_29_out, not_30_out, not_31_out, not_32_out, not_33_out,
       not_34_out, not_35_out, not_36_out, not_37_out, not_38_out, not_39_out, not_40_out, not_41_out,
       not_42_out, not_43_out, not_44_out, not_45_out, not_46_out, not_47_out;

  not not_1 (not_1_out, Op5);
  not not_2 (not_2_out, Op4);
  not not_3 (not_3_out, Op3);
  not not_4 (not_4_out, Op2);
  not not_5 (not_5_out, Op0);
  not not_6 (not_6_out, Op5);
  not not_7 (not_7_out, Op4);
  not not_8 (not_8_out, Op3);
  not not_9 (not_9_out, Op2);
  not not_10 (not_10_out, Op0);
  not not_11 (not_11_out, Op4);
  not not_12 (not_12_out, Op3);
  not not_13 (not_13_out, Op2);
  not not_14 (not_14_out, Op4);
  not not_15 (not_15_out, Op3);
  not not_16 (not_16_out, Op2);
  not not_17 (not_17_out, Op5);
  not not_18 (not_18_out, Op4);
  not not_19 (not_19_out, Op3);
  not not_20 (not_20_out, Op2);
  not not_21 (not_21_out, Op0);
  not not_22 (not_22_out, Op5);
  not not_23 (not_23_out, Op4);
  not not_24 (not_24_out, Op2);
  not not_25 (not_25_out, Op1);
  not not_26 (not_26_out, Op0);
  not not_27 (not_27_out, Op4);
  not not_28 (not_28_out, Op3);
  not not_29 (not_29_out, Op2);
  not not_30 (not_30_out, Op5);
  not not_31 (not_31_out, Op4);
  not not_32 (not_32_out, Op3);
  not not_33 (not_33_out, Op2);
  not not_34 (not_34_out, Op0);
  not not_35 (not_35_out, Op5);
  not not_36 (not_36_out, Op4);
  not not_37 (not_37_out, Op2);
  not not_38 (not_38_out, Op1);
  not not_39 (not_39_out, Op0);
  not not_40 (not_40_out, Op5);
  not not_41 (not_41_out, Op4);
  not not_42 (not_42_out, Op3);
  not not_43 (not_43_out, Op2);
  not not_44 (not_44_out, Op0);
  not not_45 (not_45_out, Op4);
  not not_46 (not_46_out, Op3);
  not not_47 (not_47_out, Op2);
  and and_1 (a, not_1_out, not_2_out, not_3_out, not_4_out, Op1, not_5_out);
  and and_2 (and_2_out, not_6_out, not_7_out, not_8_out, not_9_out, Op1, not_10_out);
  and and_3 (and_3_out, Op5, not_11_out, not_12_out, not_13_out, Op1, Op0);
  and and_4 (c, Op5, not_14_out, not_15_out, not_16_out, Op1, Op0);
  and and_5 (and_5_out, not_17_out, not_18_out, not_19_out, not_20_out, Op1, not_21_out);
  and and_6 (and_6_out, not_22_out, not_23_out, Op3, not_24_out, not_25_out, not_26_out);
  and and_7 (and_7_out, Op5, not_27_out, not_28_out, not_29_out, Op1, Op0);
  and and_8 (and_8_out, not_30_out, not_31_out, not_32_out, not_33_out, Op1, not_34_out);
  and and_9 (and_9_out, not_35_out, not_36_out, Op3, not_37_out, not_38_out, not_39_out);
  and and_10 (and_10_out, not_40_out, not_41_out, not_42_out, not_43_out, Op1, not_44_out);
  and and_11 (and_11_out, Op5, not_45_out, not_46_out, not_47_out, Op1, Op0);
  or or_1 (b, and_2_out, and_3_out);
  or or_2 (e, and_5_out, and_6_out, and_7_out);
  or or_3 (f, and_8_out, and_9_out);
  or or_4 (g, and_10_out, and_11_out);

  assign d = 1'b0;
endmodule

module display4_Rinstruction_inside (
  input  Func5,
  input  Func4,
  input  Func3,
  input  Func2,
  input  Func1,
  input  Func0,
  output a,
  output b,
  output c,
  output d,
  output e,
  output f,
  output g
);


  assign a = 1'b0;
  assign b = 1'b0;
  assign c = 1'b0;
  assign d = 1'b0;
  assign e = 1'b0;
  assign f = 1'b0;
  assign g = 1'b0;
endmodule

module ALU (
  input  ALUCtrl3,
  input  ALUCtrl2,
  input  ALUCtrl1,
  input  ALUCtrl0,
  input  [31:0] in_5,
  input  [31:0] in_6,
  output [31:0] Resultado,
  output out_8
);

  wire [1:0] aluopselector1_1_selector1;
  wire [31:0] demultiplexer_1_out0, demultiplexer_1_out1, demultiplexer_1_out2, demultiplexer_1_out3,
       demultiplexer_2_out0, demultiplexer_2_out1, demultiplexer_2_out2, demultiplexer_2_out3, Result1,
       Result2, Result3, Result4;

  Demultiplexer #(.select(2), .width(32)) demultiplexer_1 (
    .out0(demultiplexer_1_out0), .out1(demultiplexer_1_out1), .out2(demultiplexer_1_out2),
    .out3(demultiplexer_1_out3), .in(in_5), .sel(aluopselector1_1_selector1), .en(1'b1));
  Demultiplexer #(.select(2), .width(32)) demultiplexer_2 (
    .out0(demultiplexer_2_out0), .out1(demultiplexer_2_out1), .out2(demultiplexer_2_out2),
    .out3(demultiplexer_2_out3), .in(in_6), .sel(aluopselector1_1_selector1), .en(1'b1));
  ALUOpSelector1 aluopselector1_1 (
    .ALUctrl3(ALUCtrl3), .ALUctrl2(ALUCtrl2), .ALUctrl1(ALUCtrl1), .ALUctrl0(ALUCtrl0),
    .selector0(aluopselector1_1_selector1[1]), .selector1(aluopselector1_1_selector1[0]));
  assign Result1 = demultiplexer_1_out0 & demultiplexer_2_out0;  // AND_Gate AND, 32 bits wide
  assign Result2 = demultiplexer_1_out1 | demultiplexer_2_out1;  // OR_Gate OR, 32 bits wide
  Adder #(.width(32)) adder_1 (.a(demultiplexer_1_out2), .b(demultiplexer_2_out2), .out(Result3));  // open: cin, cout
  Subtractor #(.width(32)) subtractor_1 (
    .a(demultiplexer_1_out3), .b(demultiplexer_2_out3), .out(Result4));  // open: bin, bout
  assign Resultado = Result1 | Result2 | Result3 | Result4;  // OR_Gate or_2, 32 bits wide
  nor nor_1 (out_8, Resultado[0], Resultado[1], Resultado[2], Resultado[3], Resultado[4], Resultado[5], Resultado[6], Resultado[7], Resultado[8], Resultado[9], Resultado[10], Resultado[11], Resultado[12], Resultado[13], Resultado[14], Resultado[15], Resultado[16], Resultado[17], Resultado[18], Resultado[19], Resultado[20], Resultado[21], Resultado[22], Resultado[23], Resultado[24], Resultado[25], Resultado[26], Resultado[27], Resultado[28], Resultado[29], Resultado[30], Resultado[31]);
endmodule

module ALUOpSelector (
  input  ALUctrl0,
  input  ALUctrl1,
  input  ALUctrl2,
  input  ALUctrl3,
  output add,
  output \and ,
  output \or ,
  output substract
);

  wire not_1_out, not_2_out, not_3_out, not_4_out, not_5_out, not_6_out, not_7_out, not_8_out, not_9_out,
       not_10_out, not_11_out, not_12_out;

  not not_1 (not_1_out, ALUctrl0);
  not not_2 (not_2_out, ALUctrl1);
  not not_3 (not_3_out, ALUctrl3);
  not not_4 (not_4_out, ALUctrl0);
  not not_5 (not_5_out, ALUctrl1);
  not not_6 (not_6_out, ALUctrl2);
  not not_7 (not_7_out, ALUctrl3);
  not not_8 (not_8_out, ALUctrl0);
  not not_9 (not_9_out, ALUctrl1);
  not not_10 (not_10_out, ALUctrl2);
  not not_11 (not_11_out, ALUctrl0);
  not not_12 (not_12_out, ALUctrl3);
  and and_1 (add, not_1_out, not_2_out, ALUctrl2, not_3_out);
  and and_2 (\and , not_4_out, not_5_out, not_6_out, not_7_out);
  and and_3 (\or , not_8_out, not_9_out, not_10_out, ALUctrl3);
  and and_4 (substract, not_11_out, ALUctrl1, ALUctrl2, not_12_out);
endmodule

module ALUOpSelector1 (
  input  ALUctrl3,
  input  ALUctrl2,
  input  ALUctrl1,
  input  ALUctrl0,
  output selector0,
  output selector1
);

  wire and_2_out, and_3_out, not_1_out, not_2_out, not_3_out, not_4_out, not_5_out, not_6_out, not_7_out;

  not not_1 (not_1_out, ALUctrl3);
  and and_1 (selector0, not_1_out, ALUctrl1, not_2_out);
  not not_2 (not_2_out, ALUctrl0);
  not not_3 (not_3_out, ALUctrl3);
  not not_4 (not_4_out, ALUctrl2);
  not not_5 (not_5_out, ALUctrl1);
  not not_6 (not_6_out, ALUctrl3);
  not not_7 (not_7_out, ALUctrl0);
  and and_2 (and_2_out, not_3_out, not_4_out, not_5_out, ALUctrl0);
  or or_1 (selector1, and_2_out, and_3_out);
  and and_3 (and_3_out, not_6_out, ALUctrl2, ALUctrl1, not_7_out);
endmodule

module BCD_to_Decimal (
  input  D,
  input  C,
  input  B,
  input  A,
  output a_2,
  output b_2,
  output c_2,
  output d_2,
  output e,
  output f,
  output g
);

  wire and_1_out, and_2_out, and_3_out, and_4_out, and_5_out, and_6_out, and_7_out, and_8_out, and_9_out,
       and_10_out, and_11_out, and_12_out, and_13_out, and_14_out, and_15_out, and_16_out, and_17_out,
       and_18_out, and_19_out, and_20_out, and_21_out, and_22_out, and_23_out, and_24_out, and_25_out,
       and_26_out, not_1_out, not_2_out, not_3_out, not_4_out, not_5_out, not_6_out, not_7_out, not_8_out,
       not_9_out, not_10_out, not_11_out, not_12_out, not_13_out, not_14_out, not_15_out, not_16_out,
       not_17_out, not_18_out, not_19_out, not_20_out, not_21_out, not_22_out, not_23_out, not_24_out,
       not_25_out, not_26_out, not_27_out, not_28_out, not_29_out, not_30_out, not_31_out, not_32_out,
       not_33_out, not_34_out, not_35_out, not_36_out, not_37_out, not_38_out, not_39_out, not_40_out,
       not_41_out, not_42_out, not_43_out, not_44_out, not_45_out, not_46_out, not_47_out, not_48_out,
       not_49_out, not_50_out, not_51_out, not_52_out;

  not not_1 (not_1_out, D);
  not not_2 (not_2_out, C);
  and and_1 (and_1_out, not_1_out, not_2_out, not_3_out);
  not not_3 (not_3_out, A);
  not not_4 (not_4_out, D);
  and and_2 (and_2_out, not_4_out, B);
  not not_5 (not_5_out, D);
  and and_3 (and_3_out, not_5_out, C, A);
  not not_6 (not_6_out, C);
  and and_4 (and_4_out, D, not_6_out, not_7_out);
  not not_7 (not_7_out, B);
  not not_8 (not_8_out, D);
  and and_5 (and_5_out, not_8_out, not_9_out);
  not not_9 (not_9_out, C);
  not not_10 (not_10_out, D);
  not not_11 (not_11_out, B);
  and and_6 (and_6_out, not_10_out, not_11_out, not_12_out);
  not not_12 (not_12_out, A);
  not not_13 (not_13_out, C);
  and and_7 (and_7_out, not_13_out, not_14_out);
  not not_14 (not_14_out, B);
  not not_15 (not_15_out, D);
  and and_8 (and_8_out, not_15_out, B, A);
  not not_16 (not_16_out, C);
  and and_9 (and_9_out, not_16_out, not_17_out);
  not not_17 (not_17_out, B);
  not not_18 (not_18_out, D);
  and and_10 (and_10_out, not_18_out, A);
  not not_19 (not_19_out, D);
  and and_11 (and_11_out, not_19_out, C);
  not not_20 (not_20_out, D);
  not not_21 (not_21_out, C);
  not not_22 (not_22_out, A);
  not not_23 (not_23_out, D);
  not not_24 (not_24_out, C);
  not not_25 (not_25_out, D);
  not not_26 (not_26_out, A);
  not not_27 (not_27_out, D);
  not not_28 (not_28_out, B);
  not not_29 (not_29_out, C);
  not not_30 (not_30_out, B);
  not not_31 (not_31_out, C);
  and and_12 (and_12_out, not_31_out, not_32_out, not_33_out);
  not not_32 (not_32_out, B);
  not not_33 (not_33_out, A);
  not not_34 (not_34_out, D);
  and and_13 (and_13_out, not_34_out, B, not_35_out);
  not not_35 (not_35_out, A);
  not not_36 (not_36_out, D);
  and and_14 (and_14_out, not_36_out, not_37_out, not_38_out);
  not not_37 (not_37_out, B);
  not not_38 (not_38_out, A);
  not not_39 (not_39_out, D);
  and and_15 (and_15_out, not_39_out, C, not_40_out);
  not not_40 (not_40_out, B);
  not not_41 (not_41_out, D);
  and and_16 (and_16_out, not_41_out, C, not_42_out);
  not not_42 (not_42_out, A);
  and and_17 (and_17_out, D, not_43_out, not_44_out);
  not not_43 (not_43_out, C);
  not not_44 (not_44_out, B);
  not not_45 (not_45_out, D);
  not not_46 (not_46_out, C);
  and and_18 (and_18_out, not_45_out, not_46_out, B);
  not not_47 (not_47_out, D);
  and and_19 (and_19_out, not_47_out, C, not_48_out);
  not not_48 (not_48_out, B);
  not not_49 (not_49_out, D);
  and and_20 (and_20_out, not_49_out, C, not_50_out);
  not not_50 (not_50_out, A);
  not not_51 (not_51_out, C);
  and and_21 (and_21_out, D, not_51_out, not_52_out);
  not not_52 (not_52_out, B);
  or or_1 (a_2, and_1_out, and_2_out, and_3_out, and_4_out);
  or or_2 (b_2, and_5_out, and_6_out, and_7_out, and_8_out);
  or or_3 (c_2, and_9_out, and_10_out, and_11_out);
  and and_22 (and_22_out, not_20_out, not_21_out, not_22_out);
  and and_23 (and_23_out, not_23_out, not_24_out, B);
  and and_24 (and_24_out, not_25_out, B, not_26_out);
  and and_25 (and_25_out, not_27_out, C, not_28_out, A);
  and and_26 (and_26_out, D, not_29_out, not_30_out);
  or or_4 (e, and_12_out, and_13_out);
  or or_5 (f, and_14_out, and_15_out, and_16_out, and_17_out);
  or or_6 (g, and_18_out, and_19_out, and_20_out, and_21_out);
  or or_7 (d_2, and_22_out, and_23_out, and_24_out, and_25_out, and_26_out);
endmodule

module pc_counter (
  input  [7:0] in_1,
  output out_2,
  output out_3,
  output out_4,
  output out_5,
  output out_6,
  output out_7,
  output out_8,
  output out_9,
  output out_10,
  output out_11,
  output out_12,
  output out_13,
  output out_14,
  output out_15
);

  wire [7:0] divider_1_out, divider_1_rem;

  BCD_to_Decimal bcd_to_decimal_1 (
    .D(divider_1_out[3]), .C(divider_1_out[2]), .B(divider_1_out[1]), .A(divider_1_out[0]), .a_2(out_2),
    .b_2(out_3), .c_2(out_4), .d_2(out_5), .e(out_6), .f(out_7), .g(out_8));
  Divider divider_1 (.a(in_1), .b(8'ha), .out(divider_1_out), .rem(divider_1_rem));  // open: upper
  BCD_to_Decimal bcd_to_decimal_2 (
    .D(divider_1_rem[3]), .C(divider_1_rem[2]), .B(divider_1_rem[1]), .A(divider_1_rem[0]), .a_2(out_9),
    .b_2(out_10), .c_2(out_11), .d_2(out_12), .e(out_13), .f(out_14), .g(out_15));
endmodule
